// Logisim project 8 bit ALU.circ as structural Verilog: 1 circuit, main circuit ALU
module ALU (
  input  [7:0] Flag_in,
  input  [7:0] A,
  input  [7:0] B,
  input  [3:0] OpCode,
  output [7:0] Flag_Out,
  output [7:0] Result
);

  wire and_2_out, Cout, n2_1_mux_1_2_y, n4_16_decoder_1_y8, n4_16_decoder_1_y9, n4_16_decoder_1_y10,
       n4_16_decoder_1_y11, or_2_out, xnor_1_1_y, xor_1_1_y, xor_1_2_y, xor_1_3_y;
  wire [1:0] nor_2_out;
  wire [6:0] full_adder_8_1_sum;
  wire [7:0] and_1_out, Bout, left_shifter_1_out_2, n1_8_bit_extender_1_y, not_1_out, or_1_out,
       right_shifter_1_out_2, xor_8_1_y;

  Xor__8 xor_8_1 (.A(B), .B(A), .Y(xor_8_1_y));
  _1_8_Bit_extender u_1_8_bit_extender_1 (.A(Flag_Out[7]), .Y(n1_8_bit_extender_1_y));
  assign or_1_out = A | B;  // OR_Gate or_1, 8 bits wide
  Left_Shifter left_shifter_1 (.in_1(A), .out_2(left_shifter_1_out_2));
  Right_Shifter right_shifter_1 (.in_1(A), .out_2(right_shifter_1_out_2));
  _16_1_Mux__8 u_16_1_mux_8_1 (
    ._0({Flag_Out[7], full_adder_8_1_sum}), ._1({Flag_Out[7], full_adder_8_1_sum}), ._2(and_1_out),
    ._3(n1_8_bit_extender_1_y), ._4(or_1_out), ._5(xor_8_1_y), ._6(left_shifter_1_out_2),
    ._7(right_shifter_1_out_2), .out_18(Result), .in_16(OpCode), ._8({A[6:0], Flag_in[0]}),
    ._9({Flag_in[0], A[7:1]}), ._10({Flag_Out[7], full_adder_8_1_sum}),
    ._11({Flag_Out[7], full_adder_8_1_sum}));  // open: _12, _13, _14, _15
  assign not_1_out = ~B;  // NOT_Gate not_1, 8 bits wide
  _2_1_Mux__8 u_2_1_mux_8_1 (._1(not_1_out), ._0(B), .Select(OpCode[0]), .Y(Bout));
  Full_Adder__8 full_adder_8_1 (
    .Cout(Cout), .Cin(OpCode[0]), .Sum({Flag_Out[7], full_adder_8_1_sum}), .in_2(Bout), .in_3(A));
  assign and_1_out = A & B;  // AND_Gate and_1, 8 bits wide
  Xor__1 xor_1_1 (.A(B[4]), .Y(xor_1_1_y), .B(A[3]));
  _2_1_Mux__1 u_2_1_mux_1_1 (._0(xor_1_1_y), ._1(xor_1_2_y), .Select(full_adder_8_1_sum[5]), .Y(Flag_Out[4]));
  Xor__1 xor_1_2 (.A(A[3]), .Y(xor_1_2_y), .B(B[3]));
  _8_1_Parity u_8_1_parity_1 (
    .A(Result[0]), .Y(Flag_Out[2]), .B(Result[1]), .C(Result[2]), .D(Result[3]), .E(Result[4]),
    .F(Result[5]), .G(Result[6]), .H(Result[7]));
  _2_1_Mux__1 u_2_1_mux_1_2 (._0(A[7]), ._1(A[0]), .Select(OpCode[0]), .Y(n2_1_mux_1_2_y));
  nor nor_1 (Flag_Out[6], Result[0], Result[1], Result[2], Result[3], Result[4], Result[5], Result[6], Result[7]);
  _4_16_Decoder u_4_16_decoder_1 (
    .En(1'b1), .Select(OpCode), .y8(n4_16_decoder_1_y8), .y9(n4_16_decoder_1_y9), .y10(n4_16_decoder_1_y10),
    .y11(n4_16_decoder_1_y11));  // open: y0, y1, y2, y3, y4, y5, y6, y7, y12, y13, y14, y15
  XNor__1 xnor_1_1 (.A(A[7]), .Y(xnor_1_1_y), .B(Bout[7]));
  Xor__1 xor_1_3 (.A(Bout[7]), .Y(xor_1_3_y), .B(Flag_Out[7]));
  or or_2 (or_2_out, n4_16_decoder_1_y8, n4_16_decoder_1_y9);
  and and_2 (and_2_out, xnor_1_1_y, OpCode[3], xor_1_3_y);
  _4_1_Mux__1 u_4_1_mux_1_1 (
    ._0(n2_1_mux_1_2_y), ._1(and_2_out), ._2(Flag_in[0]), ._3(Cout), .Select(nor_2_out), .Y(Flag_Out[0]));
  // OR_Gate or_3 has open pins: in0=n4_16_decoder_1_y11, in1=n4_16_decoder_1_y10, out=open
  nor nor_2 (nor_2_out[0], n4_16_decoder_1_y10, or_2_out);

  assign {Flag_Out[5], Flag_Out[3], Flag_Out[1]} = 3'b001;

  // Other names for the same wires on the sheet: Fin[7:0] = Flag_in; S = Flag_Out[7]; CY = Flag_Out[0];
  //   P = Flag_Out[2]; AC = Flag_Out[4]; Z = Flag_Out[6]; OP[3:0] = OpCode

  // Notes on the sheet:
  //   Fin 0 is Carry
  //   ALU Codes:
  //   0 Add
  //   1 Subtract
  //   2 A and B
  //   3 A < B
  //   4 A or B
  //   5 A Xor B
  //   6 Shift A left
  //   7 Shift A right
  //   10 Add with carry
  //   11 Subtract with borrow
  //   8 Shift A left through carry
  //   9 Shift A right through carry
endmodule
