// Logisim project Equals.circ as structural Verilog: 2 circuits, main circuit Equals (1)
module Equals__1 (
  input  A,
  input  B,
  output Y
);

  wire and_1_out, and_2_out, nor_1_out;

  and and_1 (and_1_out, A, ~B);  // AND_Gate
  and and_2 (and_2_out, ~A, B);  // AND_Gate
  Error_to_high__1 error_to_high_1_1 (.In(nor_1_out), .Out(Y));
  nor nor_1 (nor_1_out, and_1_out, and_2_out);
endmodule

module Equals__8 (
  input  [7:0] A,
  input  [7:0] B,
  output Y
);

  wire [7:0] and_1_out, and_2_out, error_to_high_8_1_out, nor_1_out;

  assign and_1_out = A & ~B;  // AND_Gate and_1, 8 bits wide
  assign and_2_out = ~A & B;  // AND_Gate and_2, 8 bits wide
  and and_3 (Y, error_to_high_8_1_out[0], error_to_high_8_1_out[1], error_to_high_8_1_out[2], error_to_high_8_1_out[3], error_to_high_8_1_out[4], error_to_high_8_1_out[5], error_to_high_8_1_out[6], error_to_high_8_1_out[7]);
  assign nor_1_out = ~(and_1_out | and_2_out);  // NOR_Gate nor_1, 8 bits wide
  Error_to_high__8 error_to_high_8_1 (.In(nor_1_out), .Out(error_to_high_8_1_out));
endmodule
