// Logisim project Incrementer and decrementer.circ as structural Verilog: 5 circuits, main circuit Inc/dec (16)
module Inc_dec__16 (
  input  [15:0] In,
  input  Inc_Dec,
  input  Carry_Barrow_In,
  output Carry_Barrow_Out,
  output [15:0] Out
);

  wire inc_dec_2_1_carry_barrow_out, inc_dec_2_3_carry_barrow_out, inc_dec_2_4_carry_barrow_out,
       inc_dec_2_5_carry_barrow_out, inc_dec_2_6_carry_barrow_out, inc_dec_2_7_carry_barrow_out,
       inc_dec_2_8_carry_barrow_out;

  Inc_dec__2 inc_dec_2_1 (
    .In(In[13:12]), .Inc_Dec(Inc_Dec), .Carry_Barrow_In(inc_dec_2_3_carry_barrow_out),
    .Carry_Barrow_Out(inc_dec_2_1_carry_barrow_out), .Out(Out[13:12]));
  Inc_dec__2 inc_dec_2_2 (
    .In(In[15:14]), .Inc_Dec(Inc_Dec), .Carry_Barrow_In(inc_dec_2_1_carry_barrow_out),
    .Carry_Barrow_Out(Carry_Barrow_Out), .Out(Out[15:14]));
  Inc_dec__2 inc_dec_2_3 (
    .In(In[11:10]), .Inc_Dec(Inc_Dec), .Carry_Barrow_In(inc_dec_2_4_carry_barrow_out),
    .Carry_Barrow_Out(inc_dec_2_3_carry_barrow_out), .Out(Out[11:10]));
  Inc_dec__2 inc_dec_2_4 (
    .In(In[9:8]), .Inc_Dec(Inc_Dec), .Carry_Barrow_In(inc_dec_2_5_carry_barrow_out),
    .Carry_Barrow_Out(inc_dec_2_4_carry_barrow_out), .Out(Out[9:8]));
  Inc_dec__2 inc_dec_2_5 (
    .In(In[7:6]), .Inc_Dec(Inc_Dec), .Carry_Barrow_In(inc_dec_2_7_carry_barrow_out),
    .Carry_Barrow_Out(inc_dec_2_5_carry_barrow_out), .Out(Out[7:6]));
  Inc_dec__2 inc_dec_2_6 (
    .In(In[3:2]), .Inc_Dec(Inc_Dec), .Carry_Barrow_In(inc_dec_2_8_carry_barrow_out),
    .Carry_Barrow_Out(inc_dec_2_6_carry_barrow_out), .Out(Out[3:2]));
  Inc_dec__2 inc_dec_2_7 (
    .In(In[5:4]), .Inc_Dec(Inc_Dec), .Carry_Barrow_In(inc_dec_2_6_carry_barrow_out),
    .Carry_Barrow_Out(inc_dec_2_7_carry_barrow_out), .Out(Out[5:4]));
  Inc_dec__2 inc_dec_2_8 (
    .In(In[1:0]), .Inc_Dec(Inc_Dec), .Carry_Barrow_In(Carry_Barrow_In),
    .Carry_Barrow_Out(inc_dec_2_8_carry_barrow_out), .Out(Out[1:0]));
endmodule

module Inc_dec__8 (
  input  [7:0] In,
  input  Inc_Dec,
  input  Carry_Barrow_In,
  output Carry_Barrow_Out,
  output [7:0] Out
);

  wire inc_dec_2_2_carry_barrow_out, inc_dec_2_3_carry_barrow_out, inc_dec_2_4_carry_barrow_out;

  Inc_dec__2 inc_dec_2_1 (
    .In(In[7:6]), .Inc_Dec(Inc_Dec), .Carry_Barrow_In(inc_dec_2_2_carry_barrow_out),
    .Carry_Barrow_Out(Carry_Barrow_Out), .Out(Out[7:6]));
  Inc_dec__2 inc_dec_2_2 (
    .In(In[5:4]), .Inc_Dec(Inc_Dec), .Carry_Barrow_In(inc_dec_2_3_carry_barrow_out),
    .Carry_Barrow_Out(inc_dec_2_2_carry_barrow_out), .Out(Out[5:4]));
  Inc_dec__2 inc_dec_2_3 (
    .In(In[3:2]), .Inc_Dec(Inc_Dec), .Carry_Barrow_In(inc_dec_2_4_carry_barrow_out),
    .Carry_Barrow_Out(inc_dec_2_3_carry_barrow_out), .Out(Out[3:2]));
  Inc_dec__2 inc_dec_2_4 (
    .In(In[1:0]), .Inc_Dec(Inc_Dec), .Carry_Barrow_In(Carry_Barrow_In),
    .Carry_Barrow_Out(inc_dec_2_4_carry_barrow_out), .Out(Out[1:0]));
endmodule

module Inc_dec__4 (
  input  [3:0] In,
  input  Inc_Dec,
  input  Carry_Barrow_In,
  output Carry_Barrow_Out,
  output [3:0] Out
);

  wire inc_dec_2_1_carry_barrow_out;

  Inc_dec__2 inc_dec_2_1 (
    .In(In[1:0]), .Inc_Dec(Inc_Dec), .Carry_Barrow_In(Carry_Barrow_In),
    .Carry_Barrow_Out(inc_dec_2_1_carry_barrow_out), .Out(Out[1:0]));
  Inc_dec__2 inc_dec_2_2 (
    .In(In[3:2]), .Inc_Dec(Inc_Dec), .Carry_Barrow_In(inc_dec_2_1_carry_barrow_out),
    .Carry_Barrow_Out(Carry_Barrow_Out), .Out(Out[3:2]));
endmodule

module Inc_dec__2 (
  input  Inc_Dec,
  input  [1:0] In,
  input  Carry_Barrow_In,
  output Carry_Barrow_Out,
  output [1:0] Out
);

  wire not_1_out;
  wire [1:0] xnor_2_1_y, xor_2_1_y;
  wire [1:1] nor_2_out;

  nor nor_1 (Carry_Barrow_Out, xnor_2_1_y[1], xnor_2_1_y[0], not_1_out);
  nor nor_2 (nor_2_out[1], xnor_2_1_y[0], not_1_out);
  XNor__2 xnor_2_1 (.A(In), .B({2{Inc_Dec}}), .Y(xnor_2_1_y));
  not not_1 (not_1_out, Carry_Barrow_In);
  Xor__2 xor_2_1 (.A(In), .B({nor_2_out[1], Carry_Barrow_In}), .Y(xor_2_1_y));
  Error_to_Z__2 error_to_z_2_1 (.In(xor_2_1_y), .Out(Out));
endmodule

module Inc_dec__1 (
  input  IncDec,
  input  In,
  input  Carry_Barrow_In,
  output Carry_Barrow_Out,
  output Out
);

  wire and_1_out, and_2_out, and_3_out, and_4_out, not_1_out, not_2_out, not_3_out, not_4_out;

  not not_1 (not_1_out, IncDec);
  not not_2 (not_2_out, In);
  not not_3 (not_3_out, In);
  not not_4 (not_4_out, Carry_Barrow_In);
  and and_1 (and_1_out, not_1_out, In, Carry_Barrow_In);
  and and_2 (and_2_out, IncDec, not_2_out, Carry_Barrow_In);
  and and_3 (and_3_out, not_3_out, Carry_Barrow_In);
  and and_4 (and_4_out, In, not_4_out);
  or or_1 (Carry_Barrow_Out, and_1_out, and_2_out);
  or or_2 (Out, and_3_out, and_4_out);
endmodule
