// Logisim project 8-1 Parity.circ as structural Verilog: 1 circuit, main circuit 8-1 Parity
module _8_1_Parity (
  input  A,
  input  B,
  input  C,
  input  D,
  input  E,
  input  F,
  input  G,
  input  H,
  output Y
);

  wire xor_1_y, xor_2_y, xor_3_y, xor_4_y, xor_5_y, xor_6_y;

  Xor xor_1 (.A(A), .B(B), .Y(xor_1_y));
  Xor xor_2 (.A(C), .B(D), .Y(xor_2_y));
  Xor xor_3 (.A(E), .B(F), .Y(xor_3_y));
  Xor xor_4 (.A(G), .B(H), .Y(xor_4_y));
  Xor xor_5 (.A(xor_1_y), .B(xor_2_y), .Y(xor_5_y));
  Xor xor_6 (.A(xor_3_y), .B(xor_4_y), .Y(xor_6_y));
  Xor xor_7 (.A(xor_5_y), .B(xor_6_y), .Y(Y));
endmodule
