// Logisim project Z Detector.circ as structural Verilog: 6 circuits, main circuit Z Detector (1)
module Z_Detector__1 (
  input  in_1,
  output out_2
);

  Pull_Circuit pull_circuit_1 (.out_3(out_2), .P_Down(in_1), .P_Up(in_1));
endmodule

module Z_Detector__2 (
  input  [1:0] in_1,
  output [1:0] out_2
);

  Pull_Circuit pull_circuit_1 (.out_3(out_2[0]), .P_Down(in_1[0]), .P_Up(in_1[0]));
  Pull_Circuit pull_circuit_2 (.out_3(out_2[1]), .P_Down(in_1[1]), .P_Up(in_1[1]));
endmodule

module Z_Detector__4 (
  input  [3:0] in_1,
  output [3:0] out_2
);

  Pull_Circuit pull_circuit_1 (.out_3(out_2[3]), .P_Down(in_1[3]), .P_Up(in_1[3]));
  Pull_Circuit pull_circuit_2 (.out_3(out_2[2]), .P_Down(in_1[2]), .P_Up(in_1[2]));
  Pull_Circuit pull_circuit_3 (.out_3(out_2[1]), .P_Down(in_1[1]), .P_Up(in_1[1]));
  Pull_Circuit pull_circuit_4 (.out_3(out_2[0]), .P_Down(in_1[0]), .P_Up(in_1[0]));
endmodule

module Z_Detector__8 (
  input  [7:0] in_1,
  output [7:0] out_2
);

  Pull_Circuit pull_circuit_1 (.out_3(out_2[7]), .P_Down(in_1[7]), .P_Up(in_1[7]));
  Pull_Circuit pull_circuit_2 (.out_3(out_2[6]), .P_Down(in_1[6]), .P_Up(in_1[6]));
  Pull_Circuit pull_circuit_3 (.out_3(out_2[4]), .P_Down(in_1[4]), .P_Up(in_1[4]));
  Pull_Circuit pull_circuit_4 (.out_3(out_2[5]), .P_Down(in_1[5]), .P_Up(in_1[5]));
  Pull_Circuit pull_circuit_5 (.out_3(out_2[3]), .P_Down(in_1[3]), .P_Up(in_1[3]));
  Pull_Circuit pull_circuit_6 (.out_3(out_2[2]), .P_Down(in_1[2]), .P_Up(in_1[2]));
  Pull_Circuit pull_circuit_7 (.out_3(out_2[1]), .P_Down(in_1[1]), .P_Up(in_1[1]));
  Pull_Circuit pull_circuit_8 (.out_3(out_2[0]), .P_Down(in_1[0]), .P_Up(in_1[0]));
endmodule

module Z_Detector__16 (
  input  [15:0] in_1,
  output [15:0] out_2
);

  Pull_Circuit pull_circuit_1 (.out_3(out_2[15]), .P_Down(in_1[15]), .P_Up(in_1[15]));
  Pull_Circuit pull_circuit_2 (.out_3(out_2[14]), .P_Down(in_1[14]), .P_Up(in_1[14]));
  Pull_Circuit pull_circuit_3 (.out_3(out_2[13]), .P_Down(in_1[13]), .P_Up(in_1[13]));
  Pull_Circuit pull_circuit_4 (.out_3(out_2[12]), .P_Down(in_1[12]), .P_Up(in_1[12]));
  Pull_Circuit pull_circuit_5 (.out_3(out_2[11]), .P_Down(in_1[11]), .P_Up(in_1[11]));
  Pull_Circuit pull_circuit_6 (.out_3(out_2[10]), .P_Down(in_1[10]), .P_Up(in_1[10]));
  Pull_Circuit pull_circuit_7 (.out_3(out_2[8]), .P_Down(in_1[8]), .P_Up(in_1[8]));
  Pull_Circuit pull_circuit_8 (.out_3(out_2[9]), .P_Down(in_1[9]), .P_Up(in_1[9]));
  Pull_Circuit pull_circuit_9 (.out_3(out_2[7]), .P_Down(in_1[7]), .P_Up(in_1[7]));
  Pull_Circuit pull_circuit_10 (.out_3(out_2[6]), .P_Down(in_1[6]), .P_Up(in_1[6]));
  Pull_Circuit pull_circuit_11 (.out_3(out_2[5]), .P_Down(in_1[5]), .P_Up(in_1[5]));
  Pull_Circuit pull_circuit_12 (.out_3(out_2[4]), .P_Down(in_1[4]), .P_Up(in_1[4]));
  Pull_Circuit pull_circuit_13 (.out_3(out_2[2]), .P_Down(in_1[2]), .P_Up(in_1[2]));
  Pull_Circuit pull_circuit_14 (.out_3(out_2[3]), .P_Down(in_1[3]), .P_Up(in_1[3]));
  Pull_Circuit pull_circuit_15 (.out_3(out_2[1]), .P_Down(in_1[1]), .P_Up(in_1[1]));
  Pull_Circuit pull_circuit_16 (.out_3(out_2[0]), .P_Down(in_1[0]), .P_Up(in_1[0]));
endmodule

module Pull_Circuit (
  input  P_Down,
  input  P_Up,
  output out_3
);

  Xor__1 xor_1_1 (.A(P_Down), .Y(out_3), .B(P_Up));

  // Notes on the sheet:
  //   P_Down: pull=down
  //   P_Up: pull=up
endmodule
