// Logisim project 1-8 Extender.circ as structural Verilog: 1 circuit, main circuit 1-8 Bit extender
module _1_8_Bit_extender (
  input  A,
  output [7:0] Y
);


  assign Y = {{7{1'b0}}, A};
endmodule
