// Logisim project Bit Extender (1).circ as structural Verilog: 4 circuits, main circuit 1 bit extender (2)
module _1_bit_extender__16 (
  input  A,
  output [15:0] Y
);


  assign Y = {{15{1'b0}}, A};
endmodule

module _1_bit_extender__8 (
  input  A,
  output [7:0] Y
);


  assign Y = {{7{1'b0}}, A};
endmodule

module _1_bit_extender__4 (
  input  A,
  output [3:0] Y
);


  assign Y = {3'b000, A};
endmodule

module _1_bit_extender__2 (
  input  A,
  output [1:0] Y
);


  assign Y = {1'b0, A};
endmodule
