// Logisim project Bit Extender (2).circ as structural Verilog: 3 circuits, main circuit 2 bit extender (16)
module _2_bit_extender__16 (
  input  [1:0] A,
  output [15:0] Y
);


  assign Y = {{14{1'b0}}, A};
endmodule

module _2_bit_extender__8 (
  input  [1:0] A,
  output [7:0] Y
);


  assign Y = {{6{1'b0}}, A};
endmodule

module _2_bit_extender__4 (
  input  [1:0] A,
  output [3:0] Y
);


  assign Y = {2'b00, A};
endmodule
