// Logisim project Bit Extender (4).circ as structural Verilog: 2 circuits, main circuit 4 bit extender (16)
module _4_bit_extender__16 (
  input  [3:0] A,
  output [15:0] Y
);


  assign Y = {{12{1'b0}}, A};
endmodule

module _4_bit_extender__8 (
  input  [3:0] A,
  output [7:0] Y
);


  assign Y = {4'b0000, A};
endmodule
