// Logisim project Bit Extender (8).circ as structural Verilog: 1 circuit, main circuit 8 bit extender (16)
module _8_bit_extender__16 (
  input  [7:0] A,
  output [15:0] Y
);


  assign Y = {{8{1'b0}}, A};
endmodule
