// Logisim project CPU.circ as structural Verilog: 7 circuits, main circuit Main
module Pin_check (
  input  [7:0] in_1,
  input  [15:0] in_2,
  input  in_3,
  input  in_4,
  input  in_5
);

  wire main_1_d2, main_1_d3, main_1_d4, main_1_d5, main_1_out_26, main_1_out_27, main_1_out_32, main_1_out_33;

  Main main_1 (
    .D7(main_1_out_26), .D6(main_1_out_27), .in_3(main_1_d5), .in_4(main_1_d4), .in_5(main_1_d3),
    .in_6(main_1_d2), .D1(main_1_out_32), .D0(main_1_out_33), .out_26(main_1_out_26), .out_27(main_1_out_27),
    .D5(main_1_d5), .D4(main_1_d4), .D3(main_1_d3), .D2(main_1_d2), .out_32(main_1_out_32),
    .out_33(main_1_out_33));  // open: Vss, Vbb, Vcc, Vdd, Mux, Read, INTE, Write, Inc_Dec, Hold, Ready, Read_Write_Mem, Phase1, Phase2, Read_Write_into_Register, Reset, Instr_Register_Write, WR, DBIN, INT, HLDA, Wait, Sync, A15, A14, A13, A12, A11, A10, A9, A8, A7, A6, A5, A4, A3, A2, A1, A0
  RAM #(.addrWidth(16)) ram_1 ();  // open: addr, we, oe, clk, din, dout

  // Notes on the sheet:
  //   To be used for testing pin functionality
endmodule

module Main (
  input  D7,
  input  D6,
  input  in_3,
  input  in_4,
  input  in_5,
  input  in_6,
  input  D1,
  input  D0,
  input  Inc_Dec,
  input  [3:0] Read,
  input  [3:0] Write,
  input  [3:0] Mux,
  input  Instr_Register_Write,
  input  Read_Write_Mem,
  input  Read_Write_into_Register,
  input  Vss,
  input  Vbb,
  input  Vcc,
  input  Vdd,
  input  INTE,
  input  Phase2,
  input  Hold,
  input  Ready,
  input  Phase1,
  input  Reset,
  output out_26,
  output out_27,
  output D5,
  output D4,
  output D3,
  output D2,
  output out_32,
  output out_33,
  output A15,
  output A14,
  output A13,
  output A12,
  output A11,
  output A10,
  output A9,
  output A8,
  output A7,
  output A6,
  output A5,
  output A4,
  output A3,
  output A2,
  output A1,
  output A0,
  output WR,
  output HLDA,
  output Wait,
  output Sync,
  output DBIN,
  output INT
);

  wire and_1_out, Clock, l_3_8_decoder_c117a043_1_y2, l_3_8_decoder_c117a043_1_y4,
       l_3_8_decoder_c117a043_1_y5, l_3_8_decoder_c117a043_1_y6;
  wire [0:0] timing_and_control_1_registry_control_out;
  wire [1:0] timing_and_control_1_en_right_2;
  wire [2:0] timing_and_control_1_en_left;
  wire [3:0] timing_and_control_1_alu_control, timing_and_control_1_registry_control_out_2,
       timing_and_control_1_registry_control_out_3, timing_and_control_1_registry_control_out_4;
  wire [6:0] timing_and_control_1_en_right;
  wire [7:0] alu_1_flag_out_e4e05d57, alu_1_result, controlled_buffer_1_out, controlled_buffer_2_out,
       controlled_buffer_3_out, controlled_buffer_6_out, E1, E2, E3, E4, E5, E6,
       scratch_pad_49ad1382_1_bus_out;
  wire [15:0] scratch_pad_49ad1382_1_mem_bus;

  assign controlled_buffer_1_out = l_3_8_decoder_c117a043_1_y4 ? controlled_buffer_3_out : 8'bz;  // Controlled_Buffer controlled_buffer_1
  CPU_Register cpu_register_1 (.Clk(Clock), .In(controlled_buffer_1_out), .Out(E1));  // open: En
  assign controlled_buffer_2_out = l_3_8_decoder_c117a043_1_y5 ? controlled_buffer_3_out : 8'bz;  // Controlled_Buffer controlled_buffer_2
  CPU_Register cpu_register_2 (.Clk(Clock), .In(controlled_buffer_2_out), .Out(E3));  // open: En
  Accumulator_Latch accumulator_latch_1 (.In(E1), .Out(E2));  // open: Clk
  CPU_Register cpu_register_3 (.Clk(Clock), .In(alu_1_flag_out_e4e05d57), .Out(E4));  // open: En
  ALU alu_1 (
    .Flag_in_cff6aa82(E4), .A(E2), .B(E3), .OpCode(timing_and_control_1_alu_control),
    .Flag_Out_e4e05d57(alu_1_flag_out_e4e05d57), .Result(alu_1_result));
  assign controlled_buffer_3_out = l_3_8_decoder_c117a043_1_y2 ? E4 : 8'bz;  // Controlled_Buffer controlled_buffer_3
  assign controlled_buffer_3_out = l_3_8_decoder_c117a043_1_y6 ? alu_1_result : 8'bz;  // Controlled_Buffer controlled_buffer_4
  L_3_8_Decoder_c117a043 l_3_8_decoder_c117a043_1 (
    .En(1'b1), .Select(timing_and_control_1_en_left), .y2(l_3_8_decoder_c117a043_1_y2),
    .y4(l_3_8_decoder_c117a043_1_y4), .y5(l_3_8_decoder_c117a043_1_y5), .y6(l_3_8_decoder_c117a043_1_y6));  // open: y1, y3, y7, y0
  and and_1 (and_1_out, ~Vss, ~Vbb, Vcc, Vdd);  // AND_Gate
  Dual_CPU_Buffer dual_cpu_buffer_1 (
    .In0({D7, D6, in_3, in_4, in_5, in_6, D1, D0}), .In1(controlled_buffer_3_out),
    .Direction(timing_and_control_1_en_right[6]), .En(timing_and_control_1_en_right_2),
    .Out0(controlled_buffer_3_out), .Out1({D7, D6, in_3, in_4, in_5, in_6, D1, D0}));
  Timing_and_Control timing_and_control_1 (
    .INTE(INTE), .Hold(Hold), .Reg_Control_In({Inc_Dec, Mux, Read, Write}), .Ready(Ready), .Ph1(Phase1),
    .Ph2(Phase2), .Write_Instruction_Register(Instr_Register_Write),
    .Read_from_Register(Read_Write_into_Register), .Read_Write_Memory(Read_Write_Mem), .En(and_1_out),
    .Reset(Reset), .Clk(Clock), .out_20(INT), .Hold_Ack(HLDA),
    .ALU_Control(timing_and_control_1_alu_control),
    .Registry_Control_Out({timing_and_control_1_registry_control_out_4, timing_and_control_1_registry_control_out_3, timing_and_control_1_registry_control_out_2, timing_and_control_1_registry_control_out[0]}),
    .Wait(Wait),
    .En_Right({timing_and_control_1_en_right[6], timing_and_control_1_en_right_2, timing_and_control_1_en_right[3:0]}),
    .En_Left(timing_and_control_1_en_left), .Sync(Sync), .L_WR(WR), .DBIN(DBIN));
  CPU_Register cpu_register_4 (
    .En(timing_and_control_1_en_right[2]), .Clk(Clock), .In(controlled_buffer_3_out), .Out(E5));
  Instruction_Encoder_3db71ec6 instruction_encoder_3db71ec6_1 (.Data_In_9342ff20(E5));  // open: V, Encoded_Instruction_Group_74c432e9
  // Probe on controlled_buffer_3_out
  assign controlled_buffer_3_out = timing_and_control_1_en_right[1] ? scratch_pad_49ad1382_1_bus_out : 8'bz;  // Controlled_Buffer controlled_buffer_5
  assign controlled_buffer_6_out = timing_and_control_1_en_right[1] ? controlled_buffer_3_out : 8'bz;  // Controlled_Buffer controlled_buffer_6
  Scratch_Pad_49ad1382 scratch_pad_49ad1382_1 (
    .Read_Select(timing_and_control_1_registry_control_out_3),
    .Write_Select(timing_and_control_1_registry_control_out_2),
    .Bus_Read_Write(timing_and_control_1_registry_control_out_4), .Bus_In(controlled_buffer_6_out),
    .Increment_Decrement(timing_and_control_1_registry_control_out[0]), .Clock(Clock),
    .Mem_Bus(scratch_pad_49ad1382_1_mem_bus), .Bus_Out(scratch_pad_49ad1382_1_bus_out), .Error(E6));
  assign {A15, A14, A13, A12, A11, A10, A9, A8, A7, A6, A5, A4, A3, A2, A1, A0} = timing_and_control_1_en_right[0] ? scratch_pad_49ad1382_1_mem_bus : 16'bz;  // Controlled_Buffer controlled_buffer_7

  assign D2 = in_6;
  assign D3 = in_5;
  assign D4 = in_4;
  assign D5 = in_3;
  assign out_26 = D7;
  assign out_27 = D6;
  assign out_32 = D1;
  assign out_33 = D0;

  // Notes on the sheet:
  //   Reset: pull=down
  //   Any red lines here means Logisim has failed to load a register
  //   *Note: Carryover from old Logisim*
endmodule

// Register
module CPU_Register (
  input  En,
  input  Clk,
  input  [7:0] In,
  output [7:0] Out
);

  Register_8_252a90b2 register_8_252a90b2_1 (.In(In), .W(En), .Clk(Clk), .Out(Out));  // open: Clear
endmodule

module Dual_CPU_Buffer (
  input  [1:0] En,
  input  [7:0] In0,
  input  [7:0] In1,
  input  Direction,
  output [7:0] Out0,
  output [7:0] Out1
);

  wire [7:0] l_2_1_demux_8_2e02d5b2_1_l_0_f163cde3, l_2_1_demux_8_2e02d5b2_1_l_1_507cfd33,
       latch_register_8_dfa3016f_1_out, mux_8_1_y;

  Latch_Register_8_dfa3016f latch_register_8_dfa3016f_1 (
    .In(mux_8_1_y), .W(En[1]), .Out(latch_register_8_dfa3016f_1_out));  // open: Clear
  Mux_8 mux_8_1 (.p0(In0), .p1(In1), .Select(Direction), .Y(mux_8_1_y));
  assign Out0 = En[0] ? l_2_1_demux_8_2e02d5b2_1_l_0_f163cde3 : 8'bz;  // Controlled_Buffer controlled_buffer_1
  L_2_1_Demux_8_2e02d5b2 l_2_1_demux_8_2e02d5b2_1 (
    .Select(Direction), .Y(latch_register_8_dfa3016f_1_out),
    .L_0_f163cde3(l_2_1_demux_8_2e02d5b2_1_l_0_f163cde3), .L_1_507cfd33(l_2_1_demux_8_2e02d5b2_1_l_1_507cfd33));
  assign Out1 = En[0] ? l_2_1_demux_8_2e02d5b2_1_l_1_507cfd33 : 8'bz;  // Controlled_Buffer controlled_buffer_2

  // Notes on the sheet:
  //   En: pull=down
  //   0 is from top
  //   1 is from bottom
endmodule

module Accumulator_Latch (
  input  [7:0] In,
  input  Clk,
  output [7:0] Out
);

  wire and_1_out, not_1_out, z_detector_1_be9a67f0_1_out_2;

  Z_Detector_1_be9a67f0 z_detector_1_be9a67f0_1 (.in_1(In[7]), .out_2(z_detector_1_be9a67f0_1_out_2));
  not not_1 (not_1_out, z_detector_1_be9a67f0_1_out_2);
  D_Latch_3f9c06d7 d_latch_3f9c06d7_1 (.Data(In[0]), .En(and_1_out), .Output(Out[0]));  // open: Clear
  D_Latch_3f9c06d7 d_latch_3f9c06d7_2 (.Data(In[1]), .En(and_1_out), .Output(Out[1]));  // open: Clear
  D_Latch_3f9c06d7 d_latch_3f9c06d7_3 (.Data(In[2]), .En(and_1_out), .Output(Out[2]));  // open: Clear
  D_Latch_3f9c06d7 d_latch_3f9c06d7_4 (.Data(In[3]), .En(and_1_out), .Output(Out[3]));  // open: Clear
  D_Latch_3f9c06d7 d_latch_3f9c06d7_5 (.Data(In[4]), .En(and_1_out), .Output(Out[4]));  // open: Clear
  D_Latch_3f9c06d7 d_latch_3f9c06d7_6 (.Data(In[5]), .En(and_1_out), .Output(Out[5]));  // open: Clear
  D_Latch_3f9c06d7 d_latch_3f9c06d7_7 (.Data(In[6]), .En(and_1_out), .Output(Out[6]));  // open: Clear
  D_Latch_3f9c06d7 d_latch_3f9c06d7_8 (.Data(In[7]), .En(and_1_out), .Output(Out[7]));  // open: Clear
  and and_1 (and_1_out, not_1_out, Clk);

  // Notes on the sheet:
  //   Clk: pull=down
endmodule

module Timing_and_Control (
  input  Read_from_Register,
  input  Read_Write_Memory,
  input  Write_Instruction_Register,
  input  [12:0] Reg_Control_In,
  input  INTE,
  input  Ph2,
  input  Hold,
  input  En,
  input  Reset,
  input  Ph1,
  input  Ready,
  output [2:0] En_Left,
  output [6:0] En_Right,
  output Clk,
  output [3:0] ALU_Control,
  output [12:0] Registry_Control_Out,
  output L_WR,
  output Wait,
  output DBIN,
  output out_20,
  output Sync,
  output Hold_Ack
);

  wire [3:0] B, BC, C, D, DE, E, H, HL, L, M, PC, Stack, W, Z;

  Clock clock_1 (.out(Clk));
  assign M = ~4'b1001;  // NOT_Gate not_1, 4 bits wide
  assign B = ~4'b0000;  // NOT_Gate not_2, 4 bits wide
  assign C = ~4'b0001;  // NOT_Gate not_3, 4 bits wide
  assign D = ~4'b0010;  // NOT_Gate not_4, 4 bits wide
  assign E = ~4'b0011;  // NOT_Gate not_5, 4 bits wide
  assign H = ~4'b0100;  // NOT_Gate not_6, 4 bits wide
  assign L = ~4'b0101;  // NOT_Gate not_7, 4 bits wide
  assign W = ~4'b0110;  // NOT_Gate not_8, 4 bits wide
  assign Z = ~4'b0111;  // NOT_Gate not_9, 4 bits wide
  assign PC = ~4'b1000;  // NOT_Gate not_10, 4 bits wide
  assign BC = ~4'b1010;  // NOT_Gate not_11, 4 bits wide
  assign DE = ~4'b1011;  // NOT_Gate not_12, 4 bits wide
  assign HL = ~4'b1100;  // NOT_Gate not_13, 4 bits wide
  assign Stack = ~4'b1001;  // NOT_Gate not_14, 4 bits wide

  assign ALU_Control = 4'b0000;
  assign DBIN = INTE;
  assign En_Left = 3'b000;
  assign {En_Right[6:4], En_Right[2:0]} = {{3{Read_Write_Memory}}, Write_Instruction_Register, Read_from_Register, Read_Write_Memory};
  assign Hold_Ack = INTE;
  assign L_WR = INTE;
  assign out_20 = INTE;
  assign Registry_Control_Out = Reg_Control_In;
  assign Sync = INTE;
  assign Wait = INTE;
  // also tied to GND on the sheet: INTE

  // Other names for the same wires on the sheet: Read_Write_Bus[3:0] = Reg_Control_In[3:0];
  //   Read[3:0] = Reg_Control_In[7:4]; Write[3:0] = Reg_Control_In[11:8]; Increment_decrement = Reg_Control_In[12]

  // Notes on the sheet:
  //   En_Right: pull=down
  //   En_Left: pull=down
  //   Write_Instruction_Register: pull=down
  //   Read_from_Register: pull=down
  //   Read_Write_Memory: pull=down
  //   En: pull=down
  //   4 Enable latch read
  //   0 Memory Bus 1: Register Buffer
  //   6 Direction of Bus Latch
  //   Enable Bits:
  //   5 Enable latch write
  //   2 Instruction Register
endmodule

module Instruction_Decoder_and_Machine_Cycle_Encoding (
  input  [7:0] Data_In,
  output Bus_Read,
  output Bus_Write,
  output [3:0] Increment_Decrement
);

  wire [4:0] instruction_encoder_3db71ec6_1_encoded_instruction_group_74c432e9;

  Instruction_Encoder_3db71ec6 instruction_encoder_3db71ec6_1 (
    .Data_In_9342ff20(8'hc4),
    .Encoded_Instruction_Group_74c432e9(instruction_encoder_3db71ec6_1_encoded_instruction_group_74c432e9));  // open: V
  // Probe on instruction_encoder_3db71ec6_1_encoded_instruction_group_74c432e9
endmodule
