// Logisim project Instruction Encoder.circ as structural Verilog: 1 circuit, main circuit Instruction Encoder
module Instruction_Encoder (
  input  [7:0] Data_In,
  output V,
  output [4:0] Encoded_Instruction_Group
);

  wire [3:0] undriven_15, undriven_22;
  wire [3:3] undriven_14, undriven_16, undriven_21;
  wire [4:0] undriven_17, undriven_18;
  wire [4:3] undriven_19, undriven_20;
  wire [4:4] undriven_10, undriven_11, undriven_12, undriven_13;
  wire [5:0] undriven_7, undriven_24, undriven_25;
  wire [5:3] undriven, undriven_2, undriven_3, undriven_4, undriven_8;
  wire [5:4] undriven_5, undriven_6, undriven_9, undriven_23;
  wire [31:0] equals_8_32_y;

  Equals__8 equals_8_1 (.A(Data_In), .B(8'hc9), .Y(equals_8_32_y[31]));
  Equals__8 equals_8_2 (.A(Data_In), .B(8'hcd), .Y(equals_8_32_y[30]));
  _32_5_Priority_Encoder u_32_5_priority_encoder_1 (.in_1(equals_8_32_y), .Out(Encoded_Instruction_Group), .V(V));
  Equals__8 equals_8_3 (.A(Data_In), .B({2'b11, undriven, 3'b000}), .Y(equals_8_32_y[29]));
  Equals__8 equals_8_4 (.A(Data_In), .B({2'b11, undriven_2, 3'b100}), .Y(equals_8_32_y[28]));
  Equals__8 equals_8_5 (.A(Data_In), .B({2'b11, undriven_3, 3'b010}), .Y(equals_8_32_y[27]));
  Equals__8 equals_8_6 (.A(Data_In), .B(8'hc3), .Y(equals_8_32_y[26]));
  Equals__8 equals_8_7 (.A(Data_In), .B(8'h76), .Y(equals_8_32_y[24]));
  Equals__8 equals_8_8 (.A(Data_In), .B(8'he9), .Y(equals_8_32_y[25]));
  Equals__8 equals_8_9 (.A(Data_In), .B({2'b11, undriven_4, 3'b111}), .Y(equals_8_32_y[23]));
  Equals__8 equals_8_10 (.A(Data_In), .B({2'b11, undriven_5, 4'b0001}), .Y(equals_8_32_y[22]));
  Equals__8 equals_8_11 (.A(Data_In), .B({2'b11, undriven_6, 4'b0101}), .Y(equals_8_32_y[21]));
  Equals__8 equals_8_12 (.A(Data_In), .B({8{1'b0}}), .Y(equals_8_32_y[20]));
  Equals__8 equals_8_13 (.A(Data_In), .B({2'b00, undriven_8, 3'b110}), .Y(equals_8_32_y[18]));
  Equals__8 equals_8_14 (.A(Data_In), .B({2'b01, undriven_7}), .Y(equals_8_32_y[19]));
  Equals__8 equals_8_15 (.A(Data_In), .B({3'b000, undriven_10[4], 4'b0010}), .Y(equals_8_32_y[16]));
  Equals__8 equals_8_16 (.A(Data_In), .B({2'b00, undriven_9, 4'b0001}), .Y(equals_8_32_y[17]));
  Equals__8 equals_8_17 (.A(Data_In), .B({3'b001, undriven_12[4], 4'b0010}), .Y(equals_8_32_y[14]));
  Equals__8 equals_8_18 (.A(Data_In), .B({3'b000, undriven_11[4], 4'b1010}), .Y(equals_8_32_y[15]));
  Equals__8 equals_8_19 (.A(Data_In), .B({4'b1111, undriven_14[3], 3'b011}), .Y(equals_8_32_y[12]));
  Equals__8 equals_8_20 (.A(Data_In), .B({3'b001, undriven_13[4], 4'b1010}), .Y(equals_8_32_y[13]));
  Equals__8 equals_8_21 (.A(Data_In), .B({4'b1001, undriven_15}), .Y(equals_8_32_y[10]));
  Equals__8 equals_8_22 (.A(Data_In), .B(8'heb), .Y(equals_8_32_y[11]));
  Equals__8 equals_8_23 (.A(Data_In), .B({4'b1101, undriven_16[3], 3'b110}), .Y(equals_8_32_y[9]));
  Equals__8 equals_8_24 (.A(Data_In), .B({3'b101, undriven_17}), .Y(equals_8_32_y[8]));
  Equals__8 equals_8_25 (.A(Data_In), .B({3'b111, undriven_18}), .Y(equals_8_32_y[7]));
  Equals__8 equals_8_26 (.A(Data_In), .B({3'b000, undriven_19, 3'b111}), .Y(equals_8_32_y[6]));
  Equals__8 equals_8_27 (.A(Data_In), .B({3'b001, undriven_20, 3'b111}), .Y(equals_8_32_y[5]));
  Equals__8 equals_8_28 (.A(Data_In), .B({4'b1101, undriven_21[3], 3'b011}), .Y(equals_8_32_y[4]));
  Equals__8 equals_8_29 (.A(Data_In), .B({4'b1000, undriven_22}), .Y(equals_8_32_y[3]));
  Equals__8 equals_8_30 (.A(Data_In), .B({2'b00, undriven_23, 4'b1001}), .Y(equals_8_32_y[2]));
  Equals__8 equals_8_31 (.A(Data_In), .B({2'b00, undriven_24}), .Y(equals_8_32_y[1]));
  Equals__8 equals_8_32 (.A(Data_In), .B({2'b11, undriven_25}), .Y(equals_8_32_y[0]));

  // Notes on the sheet:
  //   4
  //   8
  //   12
  //   16
  //   20
  //   24
  //   28
  //   32
endmodule
