// Logisim project Scratch Pad.circ as structural Verilog: 1 circuit, main circuit Scratch Pad
module Scratch_Pad (
  input  [7:0] Bus_In,
  input  Increment_Decrement,
  input  Clock,
  input  [3:0] Bus_Read_Write,
  input  [3:0] Read_Select,
  input  [3:0] Write_Select,
  output [7:0] Bus_Out,
  output [7:0] Error,
  output [15:0] Mem_Bus
);

  wire not_2_out, not_3_out, not_6_out, not_7_out, z_detector_1_1_out_2, z_detector_1_2_out_2;
  wire [2:0] not_1_out;
  wire [3:0] not_4_out, Write_Select_t;
  wire [3:3] not_1_out_2;
  wire [7:0] B, C, controlled_buffer_2_out, controlled_buffer_5_out, D, E, H, inc_dec_8_1_out, L,
       n8_1_mux_8_1_out_10, n8_1_mux_8_2_out_10, Read_8, Write_8, Write_B, Write_BC_Pair, Write_D,
       Write_DE_Pair, Write_H, Write_HL_Pair, Write_W, Write_WZ_Pair;
  wire [15:0] Addr_Load, controlled_buffer_4_out, inc_dec_16_1_out, n8_1_mux_16_1_out_10, PC, Read_16,
       Read_WZ_Pair, Stack, Write_16, Write_PC, Write_Stack, z_detector_16_1_out_2;

  assign Read_8 = not_2_out ? n8_1_mux_8_1_out_10 : 8'bz;  // Controlled_Buffer controlled_buffer_1
  _8_1_Mux__8 u_8_1_mux_8_1 (
    ._0(B), ._1(C), ._2(D), ._3(E), ._4(H), ._5(L), ._6(Read_WZ_Pair[15:8]), ._7(Read_WZ_Pair[7:0]),
    .in_9(not_1_out), .out_10(n8_1_mux_8_1_out_10));
  assign controlled_buffer_2_out = not_3_out ? Write_8 : 8'bz;  // Controlled_Buffer controlled_buffer_2
  _8_1_Demux__8 u_8_1_demux_8_1 (
    ._0(Write_B), ._1(Write_BC_Pair), ._2(Write_D), ._3(Write_DE_Pair), .Y(controlled_buffer_2_out),
    ._4(Write_H), ._5(Write_HL_Pair), ._6(Write_W), .in_2(Write_Select_t[2:0]), ._7(Write_WZ_Pair));
  assign {not_1_out_2[3], not_1_out} = ~Read_Select;  // NOT_Gate not_1, 4 bits wide
  not not_2 (not_2_out, not_1_out_2[3]);
  not not_3 (not_3_out, Write_Select_t[3]);
  Register__16 register_16_1 (.Clk(Clock), .W(1'b1), .Out(Mem_Bus), .In(Addr_Load));  // open: Clear
  assign Read_16 = not_1_out_2[3] ? n8_1_mux_16_1_out_10 : 16'bz;  // Controlled_Buffer controlled_buffer_3
  _8_1_Mux__16 u_8_1_mux_16_1 (
    ._0({B, C}), ._1(PC), ._2({D, E}), ._3(Stack), ._4({H, L}), ._5(Mem_Bus), ._6(Read_WZ_Pair),
    .in_9(not_1_out), .out_10(n8_1_mux_16_1_out_10));  // open: _7
  assign controlled_buffer_4_out = Write_Select_t[3] ? Write_16 : 16'bz;  // Controlled_Buffer controlled_buffer_4
  _8_1_Demux__16 u_8_1_demux_16_1 (
    ._0({Write_B, Write_BC_Pair}), ._1(Write_PC), ._2({Write_D, Write_DE_Pair}), ._3(Write_Stack),
    .Y(controlled_buffer_4_out), ._4({Write_H, Write_HL_Pair}), ._5(Addr_Load),
    ._6({Write_W, Write_WZ_Pair}), .in_2(Write_Select_t[2:0]));  // open: _7
  assign not_4_out = ~Bus_Read_Write;  // NOT_Gate not_4, 4 bits wide
  assign Write_Select_t = ~Write_Select;  // NOT_Gate not_5, 4 bits wide
  assign controlled_buffer_5_out = not_4_out[3] ? Bus_In : 8'bz;  // Controlled_Buffer controlled_buffer_5
  _8_1_Demux__8 u_8_1_demux_8_2 (
    ._0(Write_B), ._1(Write_BC_Pair), ._2(Write_D), ._3(Write_DE_Pair), .Y(controlled_buffer_5_out),
    ._4(Write_H), ._5(Write_HL_Pair), ._6(Write_W), .in_2(not_4_out[2:0]), ._7(Write_WZ_Pair));
  assign Bus_Out = not_6_out ? n8_1_mux_8_2_out_10 : 8'bz;  // Controlled_Buffer controlled_buffer_6
  not not_6 (not_6_out, not_4_out[3]);
  _8_1_Mux__8 u_8_1_mux_8_2 (
    ._0(B), ._1(C), ._2(D), ._3(E), ._4(H), ._5(L), ._6(Read_WZ_Pair[15:8]), ._7(Read_WZ_Pair[7:0]),
    .in_9(not_4_out[2:0]), .out_10(n8_1_mux_8_2_out_10));
  Register__8 Tmp_W (.Clk(Clock), .In(Write_W), .Out(Read_WZ_Pair[15:8]), .W(1'b1));  // open: Clear
  Register__8 Reg__B (.Clk(Clock), .In(Write_B), .Out(B), .W(1'b1));  // open: Clear
  Register__8 Reg__D (.Clk(Clock), .In(Write_D), .Out(D), .W(1'b1));  // open: Clear
  Register__8 Reg__H (.Clk(Clock), .In(Write_H), .Out(H), .W(1'b1));  // open: Clear
  assign Write_16 = z_detector_1_1_out_2 ? Read_16 : 16'bz;  // Controlled_Buffer controlled_buffer_7
  Register__8 Tmp_Z (.Clk(Clock), .In(Write_WZ_Pair), .Out(Read_WZ_Pair[7:0]), .W(1'b1));  // open: Clear
  Register__8 Reg__C (.Clk(Clock), .In(Write_BC_Pair), .Out(C), .W(1'b1));  // open: Clear
  Register__8 Reg__E (.Clk(Clock), .In(Write_DE_Pair), .Out(E), .W(1'b1));  // open: Clear
  Register__8 Reg__L (.Clk(Clock), .In(Write_HL_Pair), .Out(L), .W(1'b1));  // open: Clear
  Z_Detector__1 z_detector_1_1 (.out_2(z_detector_1_1_out_2), .in_1(Increment_Decrement));
  assign Write_8 = z_detector_1_1_out_2 ? Read_8 : 8'bz;  // Controlled_Buffer controlled_buffer_8
  Register__16 register_16_2 (.Clk(Clock), .W(1'b1), .Out(Stack), .In(Write_Stack));  // open: Clear
  Register__16 register_16_3 (.Clk(Clock), .W(1'b1), .Out(PC), .In(Write_PC));  // open: Clear
  Inc_dec__16 inc_dec_16_1 (
    .In(Read_16), .Out(inc_dec_16_1_out), .Carry_Barrow_In(not_7_out), .Inc_Dec(Increment_Decrement));  // open: Carry_Barrow_Out
  assign Write_16 = not_7_out ? inc_dec_16_1_out : 16'bz;  // Controlled_Buffer controlled_buffer_9
  Error_Detector__16 error_detector_16_1 (.In(z_detector_16_1_out_2), .Out({Error, Error}));
  Z_Detector__16 z_detector_16_1 (.out_2(z_detector_16_1_out_2), .in_1(PC));
  Z_Detector__8 z_detector_8_1 (.out_2(Error), .in_1(D));
  Z_Detector__16 z_detector_16_2 (.out_2(z_detector_16_1_out_2), .in_1(Stack));
  Z_Detector__8 z_detector_8_2 (.out_2(Error), .in_1(B));
  Z_Detector__16 z_detector_16_3 (.out_2(z_detector_16_1_out_2), .in_1(Mem_Bus));
  Z_Detector__1 z_detector_1_2 (.out_2(z_detector_1_2_out_2), .in_1(Increment_Decrement));
  not not_7 (not_7_out, z_detector_1_2_out_2);
  Inc_dec__8 inc_dec_8_1 (
    .Inc_Dec(Increment_Decrement), .Carry_Barrow_In(not_7_out), .Out(inc_dec_8_1_out), .In(Read_8));  // open: Carry_Barrow_Out
  assign Write_8 = not_7_out ? inc_dec_8_1_out : 8'bz;  // Controlled_Buffer controlled_buffer_10
  Z_Detector__8 z_detector_8_3 (.out_2(Error), .in_1(Read_WZ_Pair[7:0]));
  Z_Detector__8 z_detector_8_4 (.out_2(Error), .in_1(L));
  Z_Detector__8 z_detector_8_5 (.out_2(Error), .in_1(E));
  Z_Detector__8 z_detector_8_6 (.out_2(Error), .in_1(Read_WZ_Pair[15:8]));
  Z_Detector__8 z_detector_8_7 (.out_2(Error), .in_1(H));
  Z_Detector__8 z_detector_8_8 (.out_2(Error), .in_1(C));

  // Other names for the same wires on the sheet: Addr_Read[15:0] = Mem_Bus; I_D = Increment_Decrement;
  //   Read_BC_Pair[15:0] = {B, C}; Read_DE_Pair[15:0] = {D, E}; Read_HL_Pair[15:0] = {H, L};
  //   Z[7:0] = Read_WZ_Pair[7:0]; W[7:0] = Read_WZ_Pair[15:8]; Write_C[7:0] = Write_BC_Pair;
  //   Write_BC_Pair[15:8] = Write_B; Write_E[7:0] = Write_DE_Pair; Write_DE_Pair[15:8] = Write_D;
  //   Write_L[7:0] = Write_HL_Pair; Write_HL_Pair[15:8] = Write_H; Write_Z[7:0] = Write_WZ_Pair;
  //   Write_WZ_Pair[15:8] = Write_W

  // Notes on the sheet:
  //   Read_Select: pull=down
  //   Bus_Read_Write: pull=down
  //   Write_Select: pull=down
  //   Pairs can only map to other 16 bit pairs/registers
endmodule
