// Logisim project Timing Phase.circ as structural Verilog: 1 circuit, main circuit Phase Timer
module Phase_Timer (
  input  Phase_1,
  input  Phase_2
);

  Clock clock_1 ();  // open: out
endmodule
