// Logisim project Timing and Control.circ as structural Verilog: 1 circuit, main circuit Timing and Control
module Timing_and_Control (
  input  Reset,
  input  INTE,
  input  Hold,
  input  Ready,
  input  Ph1,
  input  Ph2,
  input  En,
  output [2:0] En_Left,
  output [5:0] En_Right,
  output Clk,
  output [7:0] Registry_Control,
  output [3:0] ALU_Control,
  output nWR,
  output DBIN,
  output INTE_2,
  output Hold_Ack,
  output Wait,
  output Sync
);


  assign ALU_Control = 4'b0000;
  assign Clk = 1'b0;
  assign DBIN = 1'b0;
  assign En_Left = 3'b000;
  assign En_Right = {6{1'b0}};
  assign Hold_Ack = 1'b0;
  assign INTE_2 = 1'b0;
  assign nWR = 1'b0;
  assign Registry_Control = {8{1'b0}};
  assign Sync = 1'b0;
  assign Wait = 1'b0;

  // Notes on the sheet:
  //   En_Left: pull=down
  //   En_Right: pull=down
  //   En: pull=down
endmodule
