// Logisim project counter.circ as structural Verilog: 5 circuits, main circuit Counter (8)
module Counter__16 (
  input  Clk,
  input  En,
  input  Clear,
  output [15:0] Count
);

  wire and_1_out, and_2_out, and_3_out, and_4_out, and_5_out, and_6_out, and_7_out, and_8_out, and_9_out,
       and_10_out, and_11_out, and_12_out, and_13_out, and_14_out;

  JK_Flip_Flop jk_flip_flop_1 (.En(En), .K(1'b1), .J(1'b1), .Clock(Clk), .Clear(Clear), .Output(Count[0]));
  JK_Flip_Flop jk_flip_flop_2 (.En(En), .K(Count[0]), .J(Count[0]), .Clock(Clk), .Clear(Clear), .Output(Count[1]));
  and and_1 (and_1_out, Count[0], Count[1]);
  JK_Flip_Flop jk_flip_flop_3 (.En(En), .K(and_1_out), .J(and_1_out), .Clock(Clk), .Clear(Clear), .Output(Count[2]));
  and and_2 (and_2_out, and_1_out, Count[2]);
  JK_Flip_Flop jk_flip_flop_4 (.En(En), .K(and_2_out), .J(and_2_out), .Clock(Clk), .Clear(Clear), .Output(Count[3]));
  and and_3 (and_3_out, and_2_out, Count[3]);
  JK_Flip_Flop jk_flip_flop_5 (.En(En), .K(and_3_out), .J(and_3_out), .Clock(Clk), .Clear(Clear), .Output(Count[4]));
  and and_4 (and_4_out, and_3_out, Count[4]);
  JK_Flip_Flop jk_flip_flop_6 (.En(En), .K(and_4_out), .J(and_4_out), .Clock(Clk), .Clear(Clear), .Output(Count[5]));
  and and_5 (and_5_out, and_4_out, Count[5]);
  JK_Flip_Flop jk_flip_flop_7 (.En(En), .K(and_5_out), .J(and_5_out), .Clock(Clk), .Clear(Clear), .Output(Count[6]));
  and and_6 (and_6_out, and_5_out, Count[6]);
  JK_Flip_Flop jk_flip_flop_8 (.En(En), .K(and_6_out), .J(and_6_out), .Clock(Clk), .Clear(Clear), .Output(Count[7]));
  and and_7 (and_7_out, and_6_out, Count[7]);
  JK_Flip_Flop jk_flip_flop_9 (.En(En), .K(and_7_out), .J(and_7_out), .Clock(Clk), .Clear(Clear), .Output(Count[8]));
  and and_8 (and_8_out, and_7_out, Count[8]);
  JK_Flip_Flop jk_flip_flop_10 (.En(En), .K(and_8_out), .J(and_8_out), .Clock(Clk), .Clear(Clear), .Output(Count[9]));
  and and_9 (and_9_out, and_8_out, Count[9]);
  JK_Flip_Flop jk_flip_flop_11 (.En(En), .K(and_9_out), .J(and_9_out), .Clock(Clk), .Clear(Clear), .Output(Count[10]));
  and and_10 (and_10_out, and_9_out, Count[10]);
  JK_Flip_Flop jk_flip_flop_12 (
    .En(En), .K(and_10_out), .J(and_10_out), .Clock(Clk), .Clear(Clear), .Output(Count[11]));
  and and_11 (and_11_out, and_10_out, Count[11]);
  JK_Flip_Flop jk_flip_flop_13 (
    .En(En), .K(and_11_out), .J(and_11_out), .Clock(Clk), .Clear(Clear), .Output(Count[12]));
  and and_12 (and_12_out, and_11_out, Count[12]);
  JK_Flip_Flop jk_flip_flop_14 (
    .En(En), .K(and_12_out), .J(and_12_out), .Clock(Clk), .Clear(Clear), .Output(Count[13]));
  and and_13 (and_13_out, and_12_out, Count[13]);
  JK_Flip_Flop jk_flip_flop_15 (
    .En(En), .K(and_13_out), .J(and_13_out), .Clock(Clk), .Clear(Clear), .Output(Count[14]));
  and and_14 (and_14_out, and_13_out, Count[14]);
  JK_Flip_Flop jk_flip_flop_16 (
    .En(En), .K(and_14_out), .J(and_14_out), .Clock(Clk), .Clear(Clear), .Output(Count[15]));

  // Notes on the sheet:
  //   En: pull=down
  //   Clear: pull=down
endmodule

module Counter__8 (
  input  Clk,
  input  En,
  input  Clear,
  output [7:0] Count
);

  wire and_1_out, and_2_out, and_3_out, and_4_out, and_5_out, and_6_out;

  JK_Flip_Flop jk_flip_flop_1 (.En(En), .K(1'b1), .J(1'b1), .Clock(Clk), .Clear(Clear), .Output(Count[0]));
  JK_Flip_Flop jk_flip_flop_2 (.En(En), .K(Count[0]), .J(Count[0]), .Clock(Clk), .Clear(Clear), .Output(Count[1]));
  and and_1 (and_1_out, Count[0], Count[1]);
  JK_Flip_Flop jk_flip_flop_3 (.En(En), .K(and_1_out), .J(and_1_out), .Clock(Clk), .Clear(Clear), .Output(Count[2]));
  and and_2 (and_2_out, and_1_out, Count[2]);
  JK_Flip_Flop jk_flip_flop_4 (.En(En), .K(and_2_out), .J(and_2_out), .Clock(Clk), .Clear(Clear), .Output(Count[3]));
  and and_3 (and_3_out, and_2_out, Count[3]);
  JK_Flip_Flop jk_flip_flop_5 (.En(En), .K(and_3_out), .J(and_3_out), .Clock(Clk), .Clear(Clear), .Output(Count[4]));
  and and_4 (and_4_out, and_3_out, Count[4]);
  JK_Flip_Flop jk_flip_flop_6 (.En(En), .K(and_4_out), .J(and_4_out), .Clock(Clk), .Clear(Clear), .Output(Count[5]));
  and and_5 (and_5_out, and_4_out, Count[5]);
  JK_Flip_Flop jk_flip_flop_7 (.En(En), .K(and_5_out), .J(and_5_out), .Clock(Clk), .Clear(Clear), .Output(Count[6]));
  and and_6 (and_6_out, and_5_out, Count[6]);
  JK_Flip_Flop jk_flip_flop_8 (.En(En), .K(and_6_out), .J(and_6_out), .Clock(Clk), .Clear(Clear), .Output(Count[7]));

  // Notes on the sheet:
  //   En: pull=down
  //   Clear: pull=down
endmodule

module Counter__4 (
  input  Clk,
  input  En,
  input  Clear,
  output [7:0] Count
);

  wire and_1_out, and_2_out, and_3_out, and_4_out, and_5_out, and_6_out;

  JK_Flip_Flop jk_flip_flop_1 (.En(En), .K(1'b1), .J(1'b1), .Clock(Clk), .Clear(Clear), .Output(Count[0]));
  JK_Flip_Flop jk_flip_flop_2 (.En(En), .K(Count[0]), .J(Count[0]), .Clock(Clk), .Clear(Clear), .Output(Count[1]));
  and and_1 (and_1_out, Count[0], Count[1]);
  JK_Flip_Flop jk_flip_flop_3 (.En(En), .K(and_1_out), .J(and_1_out), .Clock(Clk), .Clear(Clear), .Output(Count[2]));
  and and_2 (and_2_out, and_1_out, Count[2]);
  JK_Flip_Flop jk_flip_flop_4 (.En(En), .K(and_2_out), .J(and_2_out), .Clock(Clk), .Clear(Clear), .Output(Count[3]));
  and and_3 (and_3_out, and_2_out, Count[3]);
  JK_Flip_Flop jk_flip_flop_5 (.En(En), .K(and_3_out), .J(and_3_out), .Clock(Clk), .Clear(Clear), .Output(Count[4]));
  and and_4 (and_4_out, and_3_out, Count[4]);
  JK_Flip_Flop jk_flip_flop_6 (.En(En), .K(and_4_out), .J(and_4_out), .Clock(Clk), .Clear(Clear), .Output(Count[5]));
  and and_5 (and_5_out, and_4_out, Count[5]);
  JK_Flip_Flop jk_flip_flop_7 (.En(En), .K(and_5_out), .J(and_5_out), .Clock(Clk), .Clear(Clear), .Output(Count[6]));
  and and_6 (and_6_out, and_5_out, Count[6]);
  JK_Flip_Flop jk_flip_flop_8 (.En(En), .K(and_6_out), .J(and_6_out), .Clock(Clk), .Clear(Clear), .Output(Count[7]));

  // Notes on the sheet:
  //   Clear: pull=down
  //   En: pull=down
endmodule

module Counter__2 (
  input  Clk,
  input  En,
  input  Clear,
  output [1:0] Count
);

  JK_Flip_Flop jk_flip_flop_1 (.En(En), .K(1'b1), .J(1'b1), .Clock(Clk), .Clear(Clear), .Output(Count[1]));
  JK_Flip_Flop jk_flip_flop_2 (.En(En), .K(Count[1]), .J(Count[1]), .Clock(Clk), .Clear(Clear), .Output(Count[0]));

  // Notes on the sheet:
  //   En: pull=down
  //   Clear: pull=down
endmodule

module Counter__1 (
  input  Clk,
  input  En,
  input  Clear,
  output Count
);

  JK_Flip_Flop jk_flip_flop_1 (.En(En), .K(1'b1), .J(1'b1), .Clock(Clk), .Clear(Clear), .Output(Count));

  // Notes on the sheet:
  //   En: pull=down
  //   Clear: pull=down
endmodule
