// Logisim project 16-1 Demux.circ as structural Verilog: 5 circuits, main circuit 16-1 Demux (8)
module _16_1_Demux__16 (
  input  [15:0] in_1,
  input  [3:0] in_2,
  output [15:0] _15,
  output [15:0] _0,
  output [15:0] _14,
  output [15:0] _1,
  output [15:0] _13,
  output [15:0] _2,
  output [15:0] _12,
  output [15:0] _3,
  output [15:0] _11,
  output [15:0] _4,
  output [15:0] _10,
  output [15:0] _5,
  output [15:0] _9,
  output [15:0] _6,
  output [15:0] _8,
  output [15:0] _7
);

  wire [15:0] n2_1_demux_16_1__0, n2_1_demux_16_1__1;

  _8_1_Demux__16 u_8_1_demux_16_1 (
    ._0(_8), ._1(_9), ._2(_10), ._3(_11), .Y(n2_1_demux_16_1__1), ._4(_12), ._5(_13), ._6(_14),
    .in_2(in_2[2:0]), ._7(_15));
  _2_1_Demux__16 u_2_1_demux_16_1 (._0(n2_1_demux_16_1__0), ._1(n2_1_demux_16_1__1), .Y(in_1), .Select(in_2[3]));
  _8_1_Demux__16 u_8_1_demux_16_2 (
    ._0(_0), ._1(_1), ._2(_2), ._3(_3), .Y(n2_1_demux_16_1__0), ._4(_4), ._5(_5), ._6(_6), .in_2(in_2[2:0]),
    ._7(_7));
endmodule

module _16_1_Demux__8 (
  input  [7:0] in_1,
  input  [3:0] in_2,
  output [7:0] _0,
  output [7:0] _1,
  output [7:0] _2,
  output [7:0] _3,
  output [7:0] _4,
  output [7:0] _5,
  output [7:0] _6,
  output [7:0] _7,
  output [7:0] _8,
  output [7:0] _9,
  output [7:0] _10,
  output [7:0] _11,
  output [7:0] _12,
  output [7:0] _13,
  output [7:0] _14,
  output [7:0] _15
);

  wire [7:0] n2_1_demux_8_1__0, n2_1_demux_8_1__1;

  _2_1_Demux__8 u_2_1_demux_8_1 (._1(n2_1_demux_8_1__1), ._0(n2_1_demux_8_1__0), .Select(in_2[3]), .Y(in_1));
  _8_1_Demux__8 u_8_1_demux_8_1 (
    ._0(_0), ._1(_1), ._2(_2), ._3(_3), .Y(n2_1_demux_8_1__0), ._4(_4), ._5(_5), ._6(_6), .in_2(in_2[2:0]),
    ._7(_7));
  _8_1_Demux__8 u_8_1_demux_8_2 (
    ._0(_8), ._1(_9), ._2(_10), ._3(_11), .Y(n2_1_demux_8_1__1), ._4(_12), ._5(_13), ._6(_14),
    .in_2(in_2[2:0]), ._7(_15));
endmodule

module _16_1_Demux__4 (
  input  [3:0] in_1,
  input  [3:0] in_2,
  output [3:0] _0,
  output [3:0] _1,
  output [3:0] _2,
  output [3:0] _3,
  output [3:0] _4,
  output [3:0] _5,
  output [3:0] _6,
  output [3:0] _7,
  output [3:0] _8,
  output [3:0] _9,
  output [3:0] _10,
  output [3:0] _11,
  output [3:0] _12,
  output [3:0] _13,
  output [3:0] _14,
  output [3:0] _15
);

  wire [3:0] n2_1_demux_4_1__0, n2_1_demux_4_1__1;

  _2_1_Demux__4 u_2_1_demux_4_1 (._0(n2_1_demux_4_1__0), ._1(n2_1_demux_4_1__1), .Y(in_1), .Select(in_2[3]));
  _8_1_Demux__4 u_8_1_demux_4_1 (
    ._0(_0), ._1(_1), ._2(_2), ._3(_3), .Y(n2_1_demux_4_1__0), ._4(_4), ._5(_5), ._6(_6), .in_2(in_2[2:0]),
    ._7(_7));
  _8_1_Demux__4 u_8_1_demux_4_2 (
    ._0(_8), ._1(_9), ._2(_10), ._3(_11), .Y(n2_1_demux_4_1__1), ._4(_12), ._5(_13), ._6(_14),
    .in_2(in_2[2:0]), ._7(_15));
endmodule

module _16_1_Demux__2 (
  input  [1:0] in_1,
  input  [3:0] in_2,
  output [1:0] _0,
  output [1:0] _1,
  output [1:0] _2,
  output [1:0] _3,
  output [1:0] _4,
  output [1:0] _5,
  output [1:0] _6,
  output [1:0] _7,
  output [1:0] _8,
  output [1:0] _9,
  output [1:0] _10,
  output [1:0] _11,
  output [1:0] _12,
  output [1:0] _13,
  output [1:0] _14,
  output [1:0] _15
);

  wire [1:0] n2_1_demux_2_1__0, n2_1_demux_2_1__1;

  _2_1_Demux__2 u_2_1_demux_2_1 (._0(n2_1_demux_2_1__0), ._1(n2_1_demux_2_1__1), .Y(in_1), .Select(in_2[3]));
  _8_1_Demux__2 u_8_1_demux_2_1 (
    ._0(_0), ._1(_1), ._2(_2), ._3(_3), .Y(n2_1_demux_2_1__0), ._4(_4), ._5(_5), ._6(_6), .in_2(in_2[2:0]),
    ._7(_7));
  _8_1_Demux__2 u_8_1_demux_2_2 (
    ._0(_8), ._1(_9), ._2(_10), ._3(_11), .Y(n2_1_demux_2_1__1), ._4(_12), ._5(_13), ._6(_14),
    .in_2(in_2[2:0]), ._7(_15));
endmodule

module _16_1_Demux__1 (
  input  in_1,
  input  [3:0] in_2,
  output _0,
  output _1,
  output _2,
  output _3,
  output _4,
  output _5,
  output _6,
  output _7,
  output _8,
  output _9,
  output _10,
  output _11,
  output _12,
  output _13,
  output _14,
  output _15
);

  wire n2_1_demux_1_1__0, n2_1_demux_1_1__1;

  _2_1_Demux__1 u_2_1_demux_1_1 (._0(n2_1_demux_1_1__0), ._1(n2_1_demux_1_1__1), .Y(in_1), .Select(in_2[3]));
  _8_1_Demux__1 u_8_1_demux_1_1 (
    ._0(_0), ._1(_1), ._2(_2), ._3(_3), .Y(n2_1_demux_1_1__0), ._4(_4), ._5(_5), ._6(_6), .in_2(in_2[2:0]),
    ._7(_7));
  _8_1_Demux__1 u_8_1_demux_1_2 (
    ._0(_8), ._1(_9), ._2(_10), ._3(_11), .Y(n2_1_demux_1_1__1), ._4(_12), ._5(_13), ._6(_14),
    .in_2(in_2[2:0]), ._7(_15));
endmodule
