// Logisim project 2-1 Demux.circ as structural Verilog: 5 circuits, main circuit 2-1 Demux (8)
module _2_1_Demux__16 (
  input  [15:0] Y,
  input  Select,
  output [15:0] _0,
  output [15:0] _1
);

  wire not_1_out;

  assign _0 = not_1_out ? Y : 16'bz;  // Controlled_Buffer controlled_buffer_1
  not not_1 (not_1_out, Select);
  assign _1 = Select ? Y : 16'bz;  // Controlled_Buffer controlled_buffer_2
endmodule

module _2_1_Demux__8 (
  input  [7:0] Y,
  input  Select,
  output [7:0] _0,
  output [7:0] _1
);

  wire not_1_out;

  assign _0 = not_1_out ? Y : 8'bz;  // Controlled_Buffer controlled_buffer_1
  not not_1 (not_1_out, Select);
  assign _1 = Select ? Y : 8'bz;  // Controlled_Buffer controlled_buffer_2
endmodule

module _2_1_Demux__4 (
  input  [3:0] Y,
  input  Select,
  output [3:0] _0,
  output [3:0] _1
);

  wire not_1_out;

  assign _0 = not_1_out ? Y : 4'bz;  // Controlled_Buffer controlled_buffer_1
  not not_1 (not_1_out, Select);
  assign _1 = Select ? Y : 4'bz;  // Controlled_Buffer controlled_buffer_2
endmodule

module _2_1_Demux__2 (
  input  [1:0] Y,
  input  Select,
  output [1:0] _0,
  output [1:0] _1
);

  wire not_1_out;

  assign _0 = not_1_out ? Y : 2'bz;  // Controlled_Buffer controlled_buffer_1
  not not_1 (not_1_out, Select);
  assign _1 = Select ? Y : 2'bz;  // Controlled_Buffer controlled_buffer_2
endmodule

module _2_1_Demux__1 (
  input  Y,
  input  Select,
  output _0,
  output _1
);

  wire not_1_out;

  assign _0 = not_1_out ? Y : 1'bz;  // Controlled_Buffer controlled_buffer_1
  not not_1 (not_1_out, Select);
  assign _1 = Select ? Y : 1'bz;  // Controlled_Buffer controlled_buffer_2
endmodule
