// Logisim project 4-1 Demux.circ as structural Verilog: 5 circuits, main circuit 4-1 Demux (8)
module _4_1_Demux__16 (
  input  [15:0] Y,
  input  [1:0] Select,
  output [15:0] _0,
  output [15:0] _1,
  output [15:0] _2,
  output [15:0] _3
);

  wire n2_4_decoder_1__0, n2_4_decoder_1__1, n2_4_decoder_1__2, n2_4_decoder_1__3;

  _2_4_Decoder u_2_4_decoder_1 (
    .Select(Select), .En(1'b1), ._0(n2_4_decoder_1__0), ._1(n2_4_decoder_1__1), ._2(n2_4_decoder_1__2),
    ._3(n2_4_decoder_1__3));
  assign _0 = n2_4_decoder_1__0 ? Y : 16'bz;  // Controlled_Buffer controlled_buffer_1
  assign _1 = n2_4_decoder_1__1 ? Y : 16'bz;  // Controlled_Buffer controlled_buffer_2
  assign _2 = n2_4_decoder_1__2 ? Y : 16'bz;  // Controlled_Buffer controlled_buffer_3
  assign _3 = n2_4_decoder_1__3 ? Y : 16'bz;  // Controlled_Buffer controlled_buffer_4
endmodule

module _4_1_Demux__8 (
  input  [7:0] Y,
  input  [1:0] Select,
  output [7:0] _0,
  output [7:0] _1,
  output [7:0] _2,
  output [7:0] _3
);

  wire n2_4_decoder_1__0, n2_4_decoder_1__1, n2_4_decoder_1__2, n2_4_decoder_1__3;

  _2_4_Decoder u_2_4_decoder_1 (
    .Select(Select), .En(1'b1), ._0(n2_4_decoder_1__0), ._1(n2_4_decoder_1__1), ._2(n2_4_decoder_1__2),
    ._3(n2_4_decoder_1__3));
  assign _0 = n2_4_decoder_1__0 ? Y : 8'bz;  // Controlled_Buffer controlled_buffer_1
  assign _1 = n2_4_decoder_1__1 ? Y : 8'bz;  // Controlled_Buffer controlled_buffer_2
  assign _2 = n2_4_decoder_1__2 ? Y : 8'bz;  // Controlled_Buffer controlled_buffer_3
  assign _3 = n2_4_decoder_1__3 ? Y : 8'bz;  // Controlled_Buffer controlled_buffer_4
endmodule

module _4_1_Demux__4 (
  input  [3:0] Y,
  input  [1:0] Select,
  output [3:0] _0,
  output [3:0] _1,
  output [3:0] _2,
  output [3:0] _3
);

  wire n2_4_decoder_1__0, n2_4_decoder_1__1, n2_4_decoder_1__2, n2_4_decoder_1__3;

  _2_4_Decoder u_2_4_decoder_1 (
    .Select(Select), .En(1'b1), ._0(n2_4_decoder_1__0), ._1(n2_4_decoder_1__1), ._2(n2_4_decoder_1__2),
    ._3(n2_4_decoder_1__3));
  assign _0 = n2_4_decoder_1__0 ? Y : 4'bz;  // Controlled_Buffer controlled_buffer_1
  assign _1 = n2_4_decoder_1__1 ? Y : 4'bz;  // Controlled_Buffer controlled_buffer_2
  assign _2 = n2_4_decoder_1__2 ? Y : 4'bz;  // Controlled_Buffer controlled_buffer_3
  assign _3 = n2_4_decoder_1__3 ? Y : 4'bz;  // Controlled_Buffer controlled_buffer_4
endmodule

module _4_1_Demux__2 (
  input  [1:0] Y,
  input  [1:0] Select,
  output [1:0] _0,
  output [1:0] _1,
  output [1:0] _2,
  output [1:0] _3
);

  wire n2_4_decoder_1__0, n2_4_decoder_1__1, n2_4_decoder_1__2, n2_4_decoder_1__3;

  _2_4_Decoder u_2_4_decoder_1 (
    .Select(Select), .En(1'b1), ._0(n2_4_decoder_1__0), ._1(n2_4_decoder_1__1), ._2(n2_4_decoder_1__2),
    ._3(n2_4_decoder_1__3));
  assign _0 = n2_4_decoder_1__0 ? Y : 2'bz;  // Controlled_Buffer controlled_buffer_1
  assign _1 = n2_4_decoder_1__1 ? Y : 2'bz;  // Controlled_Buffer controlled_buffer_2
  assign _2 = n2_4_decoder_1__2 ? Y : 2'bz;  // Controlled_Buffer controlled_buffer_3
  assign _3 = n2_4_decoder_1__3 ? Y : 2'bz;  // Controlled_Buffer controlled_buffer_4
endmodule

module _4_1_Demux__1 (
  input  Y,
  input  [1:0] Select,
  output _0,
  output _1,
  output _2,
  output _3
);

  wire n2_4_decoder_1__0, n2_4_decoder_1__1, n2_4_decoder_1__2, n2_4_decoder_1__3;

  _2_4_Decoder u_2_4_decoder_1 (
    .Select(Select), .En(1'b1), ._0(n2_4_decoder_1__0), ._1(n2_4_decoder_1__1), ._2(n2_4_decoder_1__2),
    ._3(n2_4_decoder_1__3));
  assign _0 = n2_4_decoder_1__0 ? Y : 1'bz;  // Controlled_Buffer controlled_buffer_1
  assign _1 = n2_4_decoder_1__1 ? Y : 1'bz;  // Controlled_Buffer controlled_buffer_2
  assign _2 = n2_4_decoder_1__2 ? Y : 1'bz;  // Controlled_Buffer controlled_buffer_3
  assign _3 = n2_4_decoder_1__3 ? Y : 1'bz;  // Controlled_Buffer controlled_buffer_4
endmodule
