// Logisim project 8-1 Demux.circ as structural Verilog: 5 circuits, main circuit 8-1 Demux (8)
module _8_1_Demux__16 (
  input  [15:0] Y,
  input  [2:0] in_2,
  output [15:0] _0,
  output [15:0] _1,
  output [15:0] _2,
  output [15:0] _3,
  output [15:0] _4,
  output [15:0] _5,
  output [15:0] _6,
  output [15:0] _7
);

  wire [15:0] n2_1_demux_16_1__0, n2_1_demux_16_1__1;

  _2_1_Demux__16 u_2_1_demux_16_1 (._0(n2_1_demux_16_1__0), ._1(n2_1_demux_16_1__1), .Y(Y), .Select(in_2[2]));
  _4_1_Demux__16 u_4_1_demux_16_1 (._0(_0), ._1(_1), .Y(n2_1_demux_16_1__0), ._2(_2), ._3(_3), .Select(in_2[1:0]));
  _4_1_Demux__16 u_4_1_demux_16_2 (._0(_4), ._1(_5), .Y(n2_1_demux_16_1__1), ._2(_6), ._3(_7), .Select(in_2[1:0]));
endmodule

module _8_1_Demux__8 (
  input  [7:0] Y,
  input  [2:0] in_2,
  output [7:0] _0,
  output [7:0] _1,
  output [7:0] _2,
  output [7:0] _3,
  output [7:0] _4,
  output [7:0] _5,
  output [7:0] _6,
  output [7:0] _7
);

  wire [7:0] n2_1_demux_8_1__0, n2_1_demux_8_1__1;

  _2_1_Demux__8 u_2_1_demux_8_1 (._1(n2_1_demux_8_1__1), ._0(n2_1_demux_8_1__0), .Select(in_2[2]), .Y(Y));
  _4_1_Demux__8 u_4_1_demux_8_1 (.Select(in_2[1:0]), ._0(_0), ._1(_1), .Y(n2_1_demux_8_1__0), ._2(_2), ._3(_3));
  _4_1_Demux__8 u_4_1_demux_8_2 (.Select(in_2[1:0]), ._0(_4), ._1(_5), .Y(n2_1_demux_8_1__1), ._2(_6), ._3(_7));
endmodule

module _8_1_Demux__4 (
  input  [3:0] Y,
  input  [2:0] in_2,
  output [3:0] _0,
  output [3:0] _1,
  output [3:0] _2,
  output [3:0] _3,
  output [3:0] _4,
  output [3:0] _5,
  output [3:0] _6,
  output [3:0] _7
);

  wire [3:0] n2_1_demux_4_1__0, n2_1_demux_4_1__1;

  _2_1_Demux__4 u_2_1_demux_4_1 (._0(n2_1_demux_4_1__0), ._1(n2_1_demux_4_1__1), .Y(Y), .Select(in_2[2]));
  _4_1_Demux__4 u_4_1_demux_4_1 (._0(_0), ._1(_1), .Y(n2_1_demux_4_1__0), ._2(_2), ._3(_3), .Select(in_2[1:0]));
  _4_1_Demux__4 u_4_1_demux_4_2 (._0(_4), ._1(_5), .Y(n2_1_demux_4_1__1), ._2(_6), ._3(_7), .Select(in_2[1:0]));
endmodule

module _8_1_Demux__2 (
  input  [1:0] Y,
  input  [2:0] in_2,
  output [1:0] _0,
  output [1:0] _1,
  output [1:0] _2,
  output [1:0] _3,
  output [1:0] _4,
  output [1:0] _5,
  output [1:0] _6,
  output [1:0] _7
);

  wire [1:0] n2_1_demux_2_1__0, n2_1_demux_2_1__1;

  _2_1_Demux__2 u_2_1_demux_2_1 (._0(n2_1_demux_2_1__0), ._1(n2_1_demux_2_1__1), .Y(Y), .Select(in_2[2]));
  _4_1_Demux__2 u_4_1_demux_2_1 (._0(_0), ._1(_1), .Y(n2_1_demux_2_1__0), ._2(_2), ._3(_3), .Select(in_2[1:0]));
  _4_1_Demux__2 u_4_1_demux_2_2 (._0(_4), ._1(_5), .Y(n2_1_demux_2_1__1), ._2(_6), ._3(_7), .Select(in_2[1:0]));
endmodule

module _8_1_Demux__1 (
  input  Y,
  input  [2:0] in_2,
  output _0,
  output _1,
  output _2,
  output _3,
  output _4,
  output _5,
  output _6,
  output _7
);

  wire n2_1_demux_1_1__0, n2_1_demux_1_1__1;

  _2_1_Demux__1 u_2_1_demux_1_1 (._0(n2_1_demux_1_1__0), ._1(n2_1_demux_1_1__1), .Y(Y), .Select(in_2[2]));
  _4_1_Demux__1 u_4_1_demux_1_1 (._0(_0), ._1(_1), ._2(_2), ._3(_3), .Select(in_2[1:0]), .Y(n2_1_demux_1_1__0));
  _4_1_Demux__1 u_4_1_demux_1_2 (._0(_4), ._1(_5), ._2(_6), ._3(_7), .Select(in_2[1:0]), .Y(n2_1_demux_1_1__1));
endmodule
