// Logisim project 1-2 Decoder.circ as structural Verilog: 1 circuit, main circuit 1-2 Decoder
module _1_2_Decoder (
  input  En,
  input  _0,
  output y0,
  output y1
);

  assign y0 = En ? ~_0 : 1'bz;  // Controlled_Inverter controlled_inverter_1
  assign y1 = En ? _0 : 1'bz;  // Controlled_Buffer controlled_buffer_1

  // Notes on the sheet:
  //   En: pull=down
endmodule
