// Logisim project Decoder.circ as structural Verilog: 4 circuits, main circuit 4-16 Decoder
module _4_16_Decoder (
  input  [3:0] Select,
  input  En,
  output _0,
  output _1,
  output _2,
  output _3,
  output _4,
  output _5,
  output _6,
  output _7,
  output _8,
  output _9,
  output _10,
  output _11,
  output _12,
  output _13,
  output _14,
  output _15
);

  wire and_1_out, and_2_out, and_3_out, and_4_out, and_5_out, and_6_out, and_7_out, and_8_out, and_9_out,
       and_10_out, and_11_out, and_12_out, and_13_out, and_14_out, and_15_out, and_16_out;

  and and_1 (and_1_out, Select[0], ~Select[1], ~Select[2], ~Select[3]);  // AND_Gate
  and and_2 (and_2_out, ~Select[0], ~Select[1], ~Select[2], ~Select[3]);  // AND_Gate
  assign _0 = En ? and_2_out : 1'bz;  // Controlled_Buffer controlled_buffer_1
  assign _1 = En ? and_1_out : 1'bz;  // Controlled_Buffer controlled_buffer_2
  and and_3 (and_3_out, ~Select[0], Select[1], ~Select[2], ~Select[3]);  // AND_Gate
  assign _2 = En ? and_3_out : 1'bz;  // Controlled_Buffer controlled_buffer_3
  and and_4 (and_4_out, ~Select[0], ~Select[1], Select[2], ~Select[3]);  // AND_Gate
  and and_5 (and_5_out, Select[0], Select[1], ~Select[2], ~Select[3]);  // AND_Gate
  assign _3 = En ? and_5_out : 1'bz;  // Controlled_Buffer controlled_buffer_4
  assign _4 = En ? and_4_out : 1'bz;  // Controlled_Buffer controlled_buffer_5
  and and_6 (and_6_out, Select[0], ~Select[1], Select[2], ~Select[3]);  // AND_Gate
  and and_7 (and_7_out, ~Select[0], Select[1], Select[2], ~Select[3]);  // AND_Gate
  assign _6 = En ? and_7_out : 1'bz;  // Controlled_Buffer controlled_buffer_6
  assign _5 = En ? and_6_out : 1'bz;  // Controlled_Buffer controlled_buffer_7
  and and_8 (and_8_out, Select[0], Select[1], Select[2], ~Select[3]);  // AND_Gate
  assign _7 = En ? and_8_out : 1'bz;  // Controlled_Buffer controlled_buffer_8
  and and_9 (and_9_out, Select[0], ~Select[1], ~Select[2], Select[3]);  // AND_Gate
  and and_10 (and_10_out, ~Select[0], ~Select[1], ~Select[2], Select[3]);  // AND_Gate
  assign _8 = En ? and_10_out : 1'bz;  // Controlled_Buffer controlled_buffer_9
  assign _9 = En ? and_9_out : 1'bz;  // Controlled_Buffer controlled_buffer_10
  and and_11 (and_11_out, ~Select[0], Select[1], ~Select[2], Select[3]);  // AND_Gate
  assign _10 = En ? and_11_out : 1'bz;  // Controlled_Buffer controlled_buffer_11
  and and_12 (and_12_out, ~Select[0], ~Select[1], Select[2], Select[3]);  // AND_Gate
  and and_13 (and_13_out, Select[0], Select[1], ~Select[2], Select[3]);  // AND_Gate
  assign _12 = En ? and_12_out : 1'bz;  // Controlled_Buffer controlled_buffer_12
  assign _11 = En ? and_13_out : 1'bz;  // Controlled_Buffer controlled_buffer_13
  and and_14 (and_14_out, ~Select[0], Select[1], Select[2], Select[3]);  // AND_Gate
  and and_15 (and_15_out, Select[0], ~Select[1], Select[2], Select[3]);  // AND_Gate
  assign _13 = En ? and_15_out : 1'bz;  // Controlled_Buffer controlled_buffer_14
  assign _14 = En ? and_14_out : 1'bz;  // Controlled_Buffer controlled_buffer_15
  and and_16 (and_16_out, Select[0], Select[1], Select[2], Select[3]);
  assign _15 = En ? and_16_out : 1'bz;  // Controlled_Buffer controlled_buffer_16

  // Notes on the sheet:
  //   En: pull=down
endmodule

module _3_8_Decoder (
  input  [2:0] Select,
  input  En,
  output _0,
  output _1,
  output _2,
  output _3,
  output _4,
  output _5,
  output _6,
  output _7
);

  wire and_1_out, and_2_out, and_3_out, and_4_out, and_5_out, and_6_out, and_7_out, and_8_out;

  and and_1 (and_1_out, ~Select[1], ~Select[2], ~Select[0]);  // AND_Gate
  assign _0 = En ? and_1_out : 1'bz;  // Controlled_Buffer controlled_buffer_1
  and and_2 (and_2_out, ~Select[1], ~Select[2], Select[0]);  // AND_Gate
  and and_3 (and_3_out, Select[1], ~Select[2], ~Select[0]);  // AND_Gate
  assign _2 = En ? and_3_out : 1'bz;  // Controlled_Buffer controlled_buffer_2
  assign _1 = En ? and_2_out : 1'bz;  // Controlled_Buffer controlled_buffer_3
  and and_4 (and_4_out, ~Select[1], Select[2], ~Select[0]);  // AND_Gate
  and and_5 (and_5_out, Select[1], ~Select[2], Select[0]);  // AND_Gate
  assign _4 = En ? and_4_out : 1'bz;  // Controlled_Buffer controlled_buffer_4
  assign _3 = En ? and_5_out : 1'bz;  // Controlled_Buffer controlled_buffer_5
  and and_6 (and_6_out, Select[1], Select[2], ~Select[0]);  // AND_Gate
  and and_7 (and_7_out, ~Select[1], Select[2], Select[0]);  // AND_Gate
  assign _6 = En ? and_6_out : 1'bz;  // Controlled_Buffer controlled_buffer_6
  assign _5 = En ? and_7_out : 1'bz;  // Controlled_Buffer controlled_buffer_7
  and and_8 (and_8_out, Select[1], Select[2], Select[0]);
  assign _7 = En ? and_8_out : 1'bz;  // Controlled_Buffer controlled_buffer_8

  // Notes on the sheet:
  //   En: pull=down
endmodule

module _2_4_Decoder (
  input  [1:0] Select,
  input  En,
  output _0,
  output _1,
  output _2,
  output _3
);

  wire and_1_out, and_2_out, and_3_out, and_4_out;

  and and_1 (and_1_out, ~Select[1], ~Select[0]);  // AND_Gate
  assign _0 = En ? and_1_out : 1'bz;  // Controlled_Buffer controlled_buffer_1
  and and_2 (and_2_out, ~Select[1], Select[0]);  // AND_Gate
  and and_3 (and_3_out, Select[1], ~Select[0]);  // AND_Gate
  assign _1 = En ? and_2_out : 1'bz;  // Controlled_Buffer controlled_buffer_2
  assign _2 = En ? and_3_out : 1'bz;  // Controlled_Buffer controlled_buffer_3
  and and_4 (and_4_out, Select[1], Select[0]);
  assign _3 = En ? and_4_out : 1'bz;  // Controlled_Buffer controlled_buffer_4

  // Notes on the sheet:
  //   En: pull=down
endmodule

module _1_2_Decoder (
  input  En,
  input  _0,
  output _0_2,
  output _1
);

  assign _0_2 = En ? ~_0 : 1'bz;  // Controlled_Inverter controlled_inverter_1
  assign _1 = En ? _0 : 1'bz;  // Controlled_Buffer controlled_buffer_1

  // Notes on the sheet:
  //   En: pull=down
endmodule
