// Logisim project Full Adder.circ as structural Verilog: 5 circuits, main circuit Full Adder (4)
module Full_Adder__1 (
  input  Cin,
  input  b2,
  input  b1,
  output Sum,
  output Cout
);

  wire and_1_out, and_2_out, xor_1_1_y;

  Xor__1 xor_1_1 (.A(b2), .Y(xor_1_1_y), .B(b1));
  and and_1 (and_1_out, b2, b1);
  Xor__1 xor_1_2 (.A(xor_1_1_y), .Y(Sum), .B(Cin));
  and and_2 (and_2_out, xor_1_1_y, Cin);
  or or_1 (Cout, and_2_out, and_1_out);

  // Notes on the sheet:
  //   Cin: pull=down
endmodule

module Full_Adder__2 (
  input  Cin,
  input  [1:0] in_2,
  input  [1:0] in_3,
  output [1:0] Sum,
  output Cout
);

  wire full_adder_1_1_cout;

  Full_Adder__1 full_adder_1_1 (.b2(in_3[0]), .b1(in_2[0]), .Sum(Sum[0]), .Cout(full_adder_1_1_cout), .Cin(Cin));
  Full_Adder__1 full_adder_1_2 (.b2(in_3[1]), .b1(in_2[1]), .Sum(Sum[1]), .Cout(Cout), .Cin(full_adder_1_1_cout));

  // Notes on the sheet:
  //   Cin: pull=down
endmodule

module Full_Adder__4 (
  input  Cin,
  input  [3:0] in_2,
  input  [3:0] in_3,
  output [3:0] Sum,
  output Cout
);

  wire full_adder_1_2_cout, full_adder_1_3_cout, full_adder_1_4_cout;

  Full_Adder__1 full_adder_1_1 (.b2(in_3[3]), .b1(in_2[3]), .Sum(Sum[3]), .Cout(Cout), .Cin(full_adder_1_2_cout));
  Full_Adder__1 full_adder_1_2 (
    .b2(in_3[2]), .b1(in_2[2]), .Sum(Sum[2]), .Cout(full_adder_1_2_cout), .Cin(full_adder_1_3_cout));
  Full_Adder__1 full_adder_1_3 (
    .b2(in_3[1]), .b1(in_2[1]), .Sum(Sum[1]), .Cout(full_adder_1_3_cout), .Cin(full_adder_1_4_cout));
  Full_Adder__1 full_adder_1_4 (.b2(in_3[0]), .b1(in_2[0]), .Sum(Sum[0]), .Cout(full_adder_1_4_cout), .Cin(Cin));

  // Notes on the sheet:
  //   Cin: pull=down
endmodule

module Full_Adder__8 (
  input  Cin,
  input  [7:0] in_2,
  input  [7:0] in_3,
  output [7:0] Sum,
  output Cout
);

  wire full_adder_1_2_cout, full_adder_1_3_cout, full_adder_1_4_cout, full_adder_1_5_cout,
       full_adder_1_6_cout, full_adder_1_7_cout, full_adder_1_8_cout;

  Full_Adder__1 full_adder_1_1 (.b2(in_3[7]), .b1(in_2[7]), .Sum(Sum[7]), .Cout(Cout), .Cin(full_adder_1_2_cout));
  Full_Adder__1 full_adder_1_2 (
    .b2(in_3[6]), .b1(in_2[6]), .Sum(Sum[6]), .Cout(full_adder_1_2_cout), .Cin(full_adder_1_3_cout));
  Full_Adder__1 full_adder_1_3 (
    .b2(in_3[5]), .b1(in_2[5]), .Sum(Sum[5]), .Cout(full_adder_1_3_cout), .Cin(full_adder_1_4_cout));
  Full_Adder__1 full_adder_1_4 (
    .b2(in_3[4]), .b1(in_2[4]), .Sum(Sum[4]), .Cout(full_adder_1_4_cout), .Cin(full_adder_1_6_cout));
  Full_Adder__1 full_adder_1_5 (
    .b2(in_3[2]), .b1(in_2[2]), .Sum(Sum[2]), .Cout(full_adder_1_5_cout), .Cin(full_adder_1_7_cout));
  Full_Adder__1 full_adder_1_6 (
    .b2(in_3[3]), .b1(in_2[3]), .Sum(Sum[3]), .Cout(full_adder_1_6_cout), .Cin(full_adder_1_5_cout));
  Full_Adder__1 full_adder_1_7 (
    .b2(in_3[1]), .b1(in_2[1]), .Sum(Sum[1]), .Cout(full_adder_1_7_cout), .Cin(full_adder_1_8_cout));
  Full_Adder__1 full_adder_1_8 (.b2(in_3[0]), .b1(in_2[0]), .Sum(Sum[0]), .Cout(full_adder_1_8_cout), .Cin(Cin));

  // Notes on the sheet:
  //   Cin: pull=down
endmodule

module Full_Adder__16 (
  input  Cin,
  input  [15:0] A,
  input  [15:0] B,
  output [15:0] Sum,
  output Cout
);

  wire full_adder_8_1_cout;

  Full_Adder__8 full_adder_8_1 (.Cout(full_adder_8_1_cout), .Cin(Cin), .Sum(Sum[7:0]), .in_2(A[7:0]), .in_3(B[7:0]));
  Full_Adder__8 full_adder_8_2 (
    .Cout(Cout), .Cin(full_adder_8_1_cout), .Sum(Sum[15:8]), .in_2(A[15:8]), .in_3(B[15:8]));

  // Notes on the sheet:
  //   Cin: pull=down
endmodule
