// Logisim project Error Detect x-1.circ as structural Verilog: 5 circuits, main circuit Error_Detector_16_889f9bab
module Error_Detector_16_889f9bab (
  input  [15:0] In,
  output Out
);

  wire or_1_out, or_2_out;
  wire [15:0] and_1_out, and_2_out, nor_1_out, undriven, undriven_2;

  Pull_Resistor pull_resistor_1 (.node(In));
  assign and_1_out = ~undriven_2 & ~undriven;  // AND_Gate and_1, 16 bits wide
  assign and_2_out = undriven_2 & undriven;  // AND_Gate and_2, 16 bits wide
  assign nor_1_out = ~(and_1_out | and_2_out);  // NOR_Gate nor_1, 16 bits wide
  or or_1 (or_1_out, nor_1_out[0], nor_1_out[1], nor_1_out[2], nor_1_out[3], nor_1_out[4], nor_1_out[5], nor_1_out[6], nor_1_out[7]);
  or or_2 (or_2_out, nor_1_out[8], nor_1_out[9], nor_1_out[10], nor_1_out[11], nor_1_out[12], nor_1_out[13], nor_1_out[14], nor_1_out[15]);
  or or_3 (Out, or_1_out, or_2_out);

  // Notes on the sheet:
  //   Works by using pull behavior to set logic
  //   Only outputs 1 on Error input
endmodule

module Error_Detector_8_e13f7c9a (
  input  [7:0] In,
  output Out
);

  wire [7:0] and_1_out, and_2_out, nor_1_out, undriven, undriven_2;

  Pull_Resistor pull_resistor_1 (.node(In));
  assign and_1_out = ~undriven_2 & ~undriven;  // AND_Gate and_1, 8 bits wide
  assign and_2_out = undriven_2 & undriven;  // AND_Gate and_2, 8 bits wide
  assign nor_1_out = ~(and_1_out | and_2_out);  // NOR_Gate nor_1, 8 bits wide
  or or_1 (Out, nor_1_out[0], nor_1_out[1], nor_1_out[2], nor_1_out[3], nor_1_out[4], nor_1_out[5], nor_1_out[6], nor_1_out[7]);

  // Notes on the sheet:
  //   Works by using pull behavior to set logic
  //   Only outputs 1 on Error input
endmodule

module Error_Detector_4_bf85b290 (
  input  [3:0] In,
  output Out
);

  wire [3:0] and_1_out, and_2_out, nor_1_out, undriven, undriven_2;

  Pull_Resistor pull_resistor_1 (.node(In));
  assign and_1_out = ~undriven_2 & ~undriven;  // AND_Gate and_1, 4 bits wide
  assign and_2_out = undriven_2 & undriven;  // AND_Gate and_2, 4 bits wide
  assign nor_1_out = ~(and_1_out | and_2_out);  // NOR_Gate nor_1, 4 bits wide
  or or_1 (Out, nor_1_out[0], nor_1_out[1], nor_1_out[2], nor_1_out[3]);

  // Notes on the sheet:
  //   Works by using pull behavior to set logic
  //   Only outputs 1 on Error input
endmodule

module Error_Detector_2_14f5d4b2 (
  input  [1:0] In,
  output Out
);

  wire [1:0] and_1_out, and_2_out, nor_1_out, undriven, undriven_2;

  Pull_Resistor pull_resistor_1 (.node(In));
  assign and_1_out = ~undriven_2 & ~undriven;  // AND_Gate and_1, 2 bits wide
  assign and_2_out = undriven_2 & undriven;  // AND_Gate and_2, 2 bits wide
  assign nor_1_out = ~(and_1_out | and_2_out);  // NOR_Gate nor_1, 2 bits wide
  or or_1 (Out, nor_1_out[0], nor_1_out[1]);

  // Notes on the sheet:
  //   Works by using pull behavior to set logic
  //   Only outputs 1 on Error input
endmodule

module Error_Detector_1_c5ec8f5b (
  input  In,
  output Out
);

  wire and_1_out, and_2_out;

  Pull_Resistor pull_resistor_1 (.node(In));
  and and_1 (and_1_out, ~In, ~In);  // AND_Gate
  and and_2 (and_2_out, In, In);
  nor nor_1 (Out, and_1_out, and_2_out);

  // Notes on the sheet:
  //   Works by using pull behavior to set logic
  //   Only outputs 1 on Error input
endmodule
