// Logisim project Error Detect.circ as structural Verilog: 5 circuits, main circuit Error Detector (1)
module Error_Detector__16 (
  input  [15:0] In,
  output [15:0] Out
);

  wire [15:0] and_1_out, and_2_out, error_to_high_16_1_out, error_to_low_16_1_out;

  Pull_Resistor pull_resistor_1 (.node(In));
  Error_to_high__16 error_to_high_16_1 (.In(In), .Out(error_to_high_16_1_out));
  Error_to_low__16 error_to_low_16_1 (.In(In), .Out(error_to_low_16_1_out));
  assign and_1_out = ~error_to_low_16_1_out & ~error_to_high_16_1_out;  // AND_Gate and_1, 16 bits wide
  assign and_2_out = error_to_low_16_1_out & error_to_high_16_1_out;  // AND_Gate and_2, 16 bits wide
  assign Out = ~(and_1_out | and_2_out);  // NOR_Gate nor_1, 16 bits wide

  // Notes on the sheet:
  //   Works by using pull behavior to set logic
  //   Only outputs 1 on Error input
endmodule

module Error_Detector__8 (
  input  [7:0] In,
  output [7:0] Out
);

  wire [7:0] and_1_out, and_2_out, error_to_high_8_1_out, error_to_low_8_1_out;

  Error_to_high__8 error_to_high_8_1 (.In(In), .Out(error_to_high_8_1_out));
  Pull_Resistor pull_resistor_1 (.node(In));
  Error_to_low__8 error_to_low_8_1 (.In(In), .Out(error_to_low_8_1_out));
  assign and_1_out = ~error_to_low_8_1_out & ~error_to_high_8_1_out;  // AND_Gate and_1, 8 bits wide
  assign and_2_out = error_to_low_8_1_out & error_to_high_8_1_out;  // AND_Gate and_2, 8 bits wide
  assign Out = ~(and_1_out | and_2_out);  // NOR_Gate nor_1, 8 bits wide

  // Notes on the sheet:
  //   Works by using pull behavior to set logic
  //   Only outputs 1 on Error input
endmodule

module Error_Detector__4 (
  input  [3:0] In,
  output [3:0] Out
);

  wire [3:0] and_1_out, and_2_out, error_to_high_4_1_out, error_to_low_4_1_out;

  Pull_Resistor pull_resistor_1 (.node(In));
  Error_to_high__4 error_to_high_4_1 (.In(In), .Out(error_to_high_4_1_out));
  Error_to_low__4 error_to_low_4_1 (.In(In), .Out(error_to_low_4_1_out));
  assign and_1_out = ~error_to_low_4_1_out & ~error_to_high_4_1_out;  // AND_Gate and_1, 4 bits wide
  assign and_2_out = error_to_low_4_1_out & error_to_high_4_1_out;  // AND_Gate and_2, 4 bits wide
  assign Out = ~(and_1_out | and_2_out);  // NOR_Gate nor_1, 4 bits wide

  // Notes on the sheet:
  //   Works by using pull behavior to set logic
  //   Only outputs 1 on Error input
endmodule

module Error_Detector__2 (
  input  [1:0] In,
  output [1:0] Out
);

  wire [1:0] and_1_out, and_2_out, error_to_high_2_1_out, error_to_low_2_1_out;

  Pull_Resistor pull_resistor_1 (.node(In));
  Error_to_high__2 error_to_high_2_1 (.In(In), .Out(error_to_high_2_1_out));
  Error_to_low__2 error_to_low_2_1 (.In(In), .Out(error_to_low_2_1_out));
  assign and_1_out = ~error_to_low_2_1_out & ~error_to_high_2_1_out;  // AND_Gate and_1, 2 bits wide
  assign and_2_out = error_to_low_2_1_out & error_to_high_2_1_out;  // AND_Gate and_2, 2 bits wide
  assign Out = ~(and_1_out | and_2_out);  // NOR_Gate nor_1, 2 bits wide

  // Notes on the sheet:
  //   Works by using pull behavior to set logic
  //   Only outputs 1 on Error input
endmodule

module Error_Detector__1 (
  input  In,
  output Out
);

  wire and_1_out, and_2_out, error_to_high_1_1_out, error_to_low_1_1_out;

  Error_to_high__1 error_to_high_1_1 (.In(In), .Out(error_to_high_1_1_out));
  Pull_Resistor pull_resistor_1 (.node(In));
  Error_to_low__1 error_to_low_1_1 (.In(In), .Out(error_to_low_1_1_out));
  and and_1 (and_1_out, ~error_to_low_1_1_out, ~error_to_high_1_1_out);  // AND_Gate
  and and_2 (and_2_out, error_to_low_1_1_out, error_to_high_1_1_out);
  nor nor_1 (Out, and_1_out, and_2_out);

  // Notes on the sheet:
  //   Works by using pull behavior to set logic
  //   Only outputs 1 on Error input
endmodule
