// Logisim project Error to High.circ as structural Verilog: 5 circuits, main circuit Error to high (1)
module Error_to_high__16 (
  input  [15:0] In,
  output [15:0] Out
);


  assign Out = In;

  // Notes on the sheet:
  //   In: pull=up
  //   Only overrides Error input
  //   Works by using pull behavior to set logic
  //   Since input is tristate, it accepts tristate input as well.
endmodule

module Error_to_high__8 (
  input  [7:0] In,
  output [7:0] Out
);


  assign Out = In;

  // Notes on the sheet:
  //   In: pull=up
  //   Only overrides Error input
  //   Works by using pull behavior to set logic
  //   Since input is tristate, it accepts tristate input as well.
endmodule

module Error_to_high__4 (
  input  [3:0] In,
  output [3:0] Out
);


  assign Out = In;

  // Notes on the sheet:
  //   In: pull=up
  //   Only overrides Error input
  //   Works by using pull behavior to set logic
  //   Since input is tristate, it accepts tristate input as well.
endmodule

module Error_to_high__2 (
  input  [1:0] In,
  output [1:0] Out
);


  assign Out = In;

  // Notes on the sheet:
  //   In: pull=up
  //   Only overrides Error input
  //   Works by using pull behavior to set logic
  //   Since input is tristate, it accepts tristate input as well.
endmodule

module Error_to_high__1 (
  input  In,
  output Out
);


  assign Out = In;

  // Notes on the sheet:
  //   In: pull=up
  //   Only overrides Error input
  //   Works by using pull behavior to set logic
  //   Since input is tristate, it accepts tristate input as well.
endmodule
