// Logisim project Error to Low.circ as structural Verilog: 5 circuits, main circuit Error to low (1)
module Error_to_low__16 (
  input  [15:0] In,
  output [15:0] Out
);


  assign Out = In;

  // Notes on the sheet:
  //   In: pull=down
  //   Only overrides Error input
  //   Works by using pull behavior to set logic
  //   Since input is tristate, it accepts tristate input as well.
endmodule

module Error_to_low__8 (
  input  [7:0] In,
  output [7:0] Out
);


  assign Out = In;

  // Notes on the sheet:
  //   In: pull=down
  //   Only overrides Error input
  //   Works by using pull behavior to set logic
  //   Since input is tristate, it accepts tristate input as well.
endmodule

module Error_to_low__4 (
  input  [3:0] In,
  output [3:0] Out
);


  assign Out = In;

  // Notes on the sheet:
  //   In: pull=down
  //   Only overrides Error input
  //   Works by using pull behavior to set logic
  //   Since input is tristate, it accepts tristate input as well.
endmodule

module Error_to_low__2 (
  input  [1:0] In,
  output [1:0] Out
);


  assign Out = In;

  // Notes on the sheet:
  //   In: pull=down
  //   Only overrides Error input
  //   Works by using pull behavior to set logic
  //   Since input is tristate, it accepts tristate input as well.
endmodule

module Error_to_low__1 (
  input  In,
  output Out
);


  assign Out = In;

  // Notes on the sheet:
  //   In: pull=down
  //   Only overrides Error input
  //   Works by using pull behavior to set logic
  //   Since input is tristate, it accepts tristate input as well.
endmodule
