// Logisim project Error to Z.circ as structural Verilog: 5 circuits, main circuit Error to Z (1)
module Error_to_Z__16 (
  input  [15:0] In,
  output [15:0] Out
);

  wire error_detector_1_1_out, not_1_out;

  not not_1 (not_1_out, error_detector_1_1_out);
  Error_Detector__1 error_detector_1_1 (.In(In[0]), .Out(error_detector_1_1_out));
  assign Out = not_1_out ? In : 16'bz;  // Controlled_Buffer controlled_buffer_1

  // Notes on the sheet:
  //   Only overrides Error input
  //   Since input is tristate, it accepts tristate input as well.
endmodule

module Error_to_Z__8 (
  input  [7:0] In,
  output [7:0] Out
);

  wire error_detector_1_1_out, not_1_out;

  not not_1 (not_1_out, error_detector_1_1_out);
  Error_Detector__1 error_detector_1_1 (.In(In[0]), .Out(error_detector_1_1_out));
  assign Out = not_1_out ? In : 8'bz;  // Controlled_Buffer controlled_buffer_1

  // Notes on the sheet:
  //   Only overrides Error input
  //   Since input is tristate, it accepts tristate input as well.
endmodule

module Error_to_Z__4 (
  input  [3:0] In,
  output [3:0] Out
);

  wire error_detector_1_1_out, not_1_out;

  Error_Detector__1 error_detector_1_1 (.In(In[0]), .Out(error_detector_1_1_out));
  not not_1 (not_1_out, error_detector_1_1_out);
  assign Out = not_1_out ? In : 4'bz;  // Controlled_Buffer controlled_buffer_1

  // Notes on the sheet:
  //   Since input is tristate, it accepts tristate input as well.
  //   Only overrides Error input
endmodule

module Error_to_Z__2 (
  input  [1:0] In,
  output [1:0] Out
);

  wire error_detector_1_1_out, not_1_out;

  Error_Detector__1 error_detector_1_1 (.In(In[0]), .Out(error_detector_1_1_out));
  not not_1 (not_1_out, error_detector_1_1_out);
  assign Out = not_1_out ? In : 2'bz;  // Controlled_Buffer controlled_buffer_1

  // Notes on the sheet:
  //   Only overrides Error input
  //   Since input is tristate, it accepts tristate input as well.
endmodule

module Error_to_Z__1 (
  input  In,
  output Out
);

  wire error_detector_1_1_out, not_1_out;

  Error_Detector__1 error_detector_1_1 (.In(In), .Out(error_detector_1_1_out));
  not not_1 (not_1_out, error_detector_1_1_out);
  assign Out = not_1_out ? In : 1'bz;  // Controlled_Buffer controlled_buffer_1

  // Notes on the sheet:
  //   Only overrides Error input
  //   Since input is tristate, it accepts tristate input as well.
endmodule
