// Logisim project 16-1 Mux.circ as structural Verilog: 5 circuits, main circuit Mux_16
module Mux_16 (
  input  [15:0] p0,
  input  [15:0] p15,
  input  [15:0] p1,
  input  [15:0] p14,
  input  [15:0] p2,
  input  [15:0] p13,
  input  [15:0] p3,
  input  [15:0] p12,
  input  [15:0] p4,
  input  [15:0] p11,
  input  [15:0] p5,
  input  [15:0] p10,
  input  [15:0] p6,
  input  [15:0] p9,
  input  [15:0] p7,
  input  [15:0] p8,
  input  [3:0] in_17,
  output [15:0] out_18
);

  wire [15:0] mux_16_1_o, mux_16_3_o;

  _8_1_Mux_Mux_16 mux_16_1 (
    .p2(p2), .p3(p3), .p4(p4), .p0(p0), .p1(p1), .s(in_17[2:0]), .p5(p5), .p6(p6), .p7(p7), .o(mux_16_1_o));
  _2_1_Mux_Mux_16 mux_16_2 (.p0(mux_16_1_o), .p1(mux_16_3_o), .Select(in_17[3]), .Y(out_18));
  _8_1_Mux_Mux_16 mux_16_3 (
    .p2(p10), .p3(p11), .p4(p12), .p0(p8), .p1(p9), .s(in_17[2:0]), .p5(p13), .p6(p14), .p7(p15),
    .o(mux_16_3_o));
endmodule

module Mux_8 (
  input  [7:0] p0,
  input  [7:0] p1,
  input  [7:0] p2,
  input  [7:0] p3,
  input  [7:0] p4,
  input  [7:0] p5,
  input  [7:0] p6,
  input  [7:0] p7,
  input  [7:0] p8,
  input  [7:0] p9,
  input  [7:0] p10,
  input  [7:0] p11,
  input  [7:0] p12,
  input  [7:0] p13,
  input  [7:0] p14,
  input  [3:0] in_16,
  input  [7:0] p15,
  output [7:0] out_18
);

  wire [7:0] mux_8_1_out_10, mux_8_2_out_10;

  _8_1_Mux_Mux_8 mux_8_1 (
    .in_9(in_16[2:0]), .p4(p4), .p5(p5), .p6(p6), .p7(p7), .p0(p0), .p1(p1), .p2(p2), .p3(p3),
    .out_10(mux_8_1_out_10));
  _8_1_Mux_Mux_8 mux_8_2 (
    .in_9(in_16[2:0]), .p4(p12), .p5(p13), .p6(p14), .p7(p15), .p0(p8), .p1(p9), .p2(p10), .p3(p11),
    .out_10(mux_8_2_out_10));
  _2_1_Mux_Mux_8 mux_8_3 (.p0(mux_8_1_out_10), .p1(mux_8_2_out_10), .Select(in_16[3]), .Y(out_18));
endmodule

module Mux_4 (
  input  [3:0] p0,
  input  [3:0] p1,
  input  [3:0] p2,
  input  [3:0] p3,
  input  [3:0] p4,
  input  [3:0] p5,
  input  [3:0] p6,
  input  [3:0] p7,
  input  [3:0] p8,
  input  [3:0] p9,
  input  [3:0] p10,
  input  [3:0] p11,
  input  [3:0] p12,
  input  [3:0] p13,
  input  [3:0] p14,
  input  [3:0] in_16,
  input  [3:0] p15,
  output [3:0] out_18
);

  wire [3:0] mux_4_1_out_10, mux_4_2_out_10;

  _8_1_Mux_Mux_4 mux_4_1 (
    .in_9(in_16[2:0]), .p4(p4), .p5(p5), .p6(p6), .p7(p7), .p0(p0), .p1(p1), .p2(p2), .p3(p3),
    .out_10(mux_4_1_out_10));
  _8_1_Mux_Mux_4 mux_4_2 (
    .in_9(in_16[2:0]), .p4(p12), .p5(p13), .p6(p14), .p7(p15), .p0(p8), .p1(p9), .p2(p10), .p3(p11),
    .out_10(mux_4_2_out_10));
  _2_1_Mux_Mux_4 mux_4_3 (.p0(mux_4_1_out_10), .p1(mux_4_2_out_10), .Select(in_16[3]), .Y(out_18));
endmodule

module Mux_2 (
  input  [1:0] p0,
  input  [1:0] p1,
  input  [1:0] p2,
  input  [1:0] p3,
  input  [1:0] p4,
  input  [1:0] p5,
  input  [1:0] p6,
  input  [1:0] p7,
  input  [1:0] p8,
  input  [1:0] p9,
  input  [1:0] p10,
  input  [1:0] p11,
  input  [1:0] p12,
  input  [1:0] p13,
  input  [1:0] p14,
  input  [3:0] in_16,
  input  [1:0] p15,
  output [1:0] out_18
);

  wire [1:0] mux_2_1_out_10, mux_2_2_out_10;

  _8_1_Mux_Mux_2 mux_2_1 (
    .in_9(in_16[2:0]), .p4(p4), .p5(p5), .p6(p6), .p7(p7), .p0(p0), .p1(p1), .p2(p2), .p3(p3),
    .out_10(mux_2_1_out_10));
  _8_1_Mux_Mux_2 mux_2_2 (
    .in_9(in_16[2:0]), .p4(p12), .p5(p13), .p6(p14), .p7(p15), .p0(p8), .p1(p9), .p2(p10), .p3(p11),
    .out_10(mux_2_2_out_10));
  _2_1_Mux_Mux_2 mux_2_3 (.p0(mux_2_1_out_10), .p1(mux_2_2_out_10), .Select(in_16[3]), .Y(out_18));
endmodule

module Mux_1 (
  input  p0,
  input  p1,
  input  p2,
  input  p3,
  input  p4,
  input  p5,
  input  p6,
  input  p7,
  input  p8,
  input  p9,
  input  p10,
  input  p11,
  input  p12,
  input  p13,
  input  p14,
  input  [3:0] in_16,
  input  p15,
  output out_18
);

  wire mux_1_1_out_10, mux_1_2_out_10;

  _8_1_Mux_Mux_1 mux_1_1 (
    .in_9(in_16[2:0]), .p4(p4), .p5(p5), .p6(p6), .p7(p7), .p0(p0), .p1(p1), .p2(p2), .p3(p3),
    .out_10(mux_1_1_out_10));
  _8_1_Mux_Mux_1 mux_1_2 (
    .in_9(in_16[2:0]), .p4(p12), .p5(p13), .p6(p14), .p7(p15), .p0(p8), .p1(p9), .p2(p10), .p3(p11),
    .out_10(mux_1_2_out_10));
  _2_1_Mux_Mux_1 mux_1_3 (.p0(mux_1_1_out_10), .p1(mux_1_2_out_10), .Select(in_16[3]), .Y(out_18));
endmodule
