// Logisim project 2-1 Mux.circ as structural Verilog: 5 circuits, main circuit Mux_16
module Mux_16 (
  input  [15:0] p0,
  input  [15:0] p1,
  input  Select,
  output [15:0] Y
);

  wire [15:0] and_1_out, and_2_out, not_1_out;

  assign not_1_out = ~{16{Select}};  // NOT_Gate not_1, 16 bits wide
  assign and_1_out = p0 & not_1_out;  // AND_Gate and_1, 16 bits wide
  assign and_2_out = p1 & {16{Select}};  // AND_Gate and_2, 16 bits wide
  assign Y = and_1_out | and_2_out;  // OR_Gate or_1, 16 bits wide
endmodule

module Mux_8 (
  input  [7:0] p0,
  input  [7:0] p1,
  input  Select,
  output [7:0] Y
);

  wire [7:0] and_1_out, and_2_out, not_1_out;

  assign not_1_out = ~{8{Select}};  // NOT_Gate not_1, 8 bits wide
  assign and_1_out = p0 & not_1_out;  // AND_Gate and_1, 8 bits wide
  assign and_2_out = p1 & {8{Select}};  // AND_Gate and_2, 8 bits wide
  assign Y = and_1_out | and_2_out;  // OR_Gate or_1, 8 bits wide
endmodule

module Mux_4 (
  input  [3:0] p0,
  input  [3:0] p1,
  input  Select,
  output [3:0] Y
);

  wire [3:0] and_1_out, and_2_out, not_1_out;

  assign not_1_out = ~{4{Select}};  // NOT_Gate not_1, 4 bits wide
  assign and_1_out = p0 & not_1_out;  // AND_Gate and_1, 4 bits wide
  assign and_2_out = p1 & {4{Select}};  // AND_Gate and_2, 4 bits wide
  assign Y = and_1_out | and_2_out;  // OR_Gate or_1, 4 bits wide
endmodule

module Mux_2 (
  input  [1:0] p0,
  input  [1:0] p1,
  input  Select,
  output [1:0] Y
);

  wire [1:0] and_1_out, and_2_out, not_1_out;

  assign not_1_out = ~{2{Select}};  // NOT_Gate not_1, 2 bits wide
  assign and_1_out = p0 & not_1_out;  // AND_Gate and_1, 2 bits wide
  assign and_2_out = p1 & {2{Select}};  // AND_Gate and_2, 2 bits wide
  assign Y = and_1_out | and_2_out;  // OR_Gate or_1, 2 bits wide
endmodule

module Mux_1 (
  input  p0,
  input  p1,
  input  Select,
  output Y
);

  wire and_1_out, and_2_out, not_1_out;

  not not_1 (not_1_out, Select);
  and and_1 (and_1_out, p0, not_1_out);
  and and_2 (and_2_out, p1, Select);
  or or_1 (Y, and_1_out, and_2_out);
endmodule
