// Logisim project 4-1 Mux.circ as structural Verilog: 5 circuits, main circuit Mux_16
module Mux_16 (
  input  [15:0] p0,
  input  [15:0] p1,
  input  [15:0] p2,
  input  [15:0] p3,
  input  [1:0] Select,
  output [15:0] Y
);

  wire [15:0] and_1_out, and_2_out, and_3_out, and_4_out, not_1_out, not_2_out, not_3_out, not_4_out;

  assign not_1_out = ~{16{Select[0]}};  // NOT_Gate not_1, 16 bits wide
  assign not_2_out = ~{16{Select[1]}};  // NOT_Gate not_2, 16 bits wide
  assign not_3_out = ~{16{Select[0]}};  // NOT_Gate not_3, 16 bits wide
  assign not_4_out = ~{16{Select[1]}};  // NOT_Gate not_4, 16 bits wide
  assign and_1_out = p0 & not_1_out & not_2_out;  // AND_Gate and_1, 16 bits wide
  assign and_2_out = p2 & not_3_out & {16{Select[1]}};  // AND_Gate and_2, 16 bits wide
  assign and_3_out = p1 & {16{Select[0]}} & not_4_out;  // AND_Gate and_3, 16 bits wide
  assign and_4_out = p3 & {16{Select[0]}} & {16{Select[1]}};  // AND_Gate and_4, 16 bits wide
  assign Y = and_1_out | and_2_out | and_3_out | and_4_out;  // OR_Gate or_1, 16 bits wide
endmodule

module Mux_8 (
  input  [7:0] p0,
  input  [7:0] p1,
  input  [7:0] p2,
  input  [7:0] p3,
  input  [1:0] Select,
  output [7:0] Y
);

  wire [7:0] and_1_out, and_2_out, and_3_out, and_4_out, not_1_out, not_2_out, not_3_out, not_4_out;

  assign not_1_out = ~{8{Select[0]}};  // NOT_Gate not_1, 8 bits wide
  assign not_2_out = ~{8{Select[1]}};  // NOT_Gate not_2, 8 bits wide
  assign not_3_out = ~{8{Select[0]}};  // NOT_Gate not_3, 8 bits wide
  assign not_4_out = ~{8{Select[1]}};  // NOT_Gate not_4, 8 bits wide
  assign and_1_out = p0 & not_1_out & not_2_out;  // AND_Gate and_1, 8 bits wide
  assign and_2_out = p2 & not_3_out & {8{Select[1]}};  // AND_Gate and_2, 8 bits wide
  assign and_3_out = p1 & {8{Select[0]}} & not_4_out;  // AND_Gate and_3, 8 bits wide
  assign and_4_out = p3 & {8{Select[0]}} & {8{Select[1]}};  // AND_Gate and_4, 8 bits wide
  assign Y = and_1_out | and_2_out | and_3_out | and_4_out;  // OR_Gate or_1, 8 bits wide
endmodule

module Mux_4 (
  input  [3:0] p0,
  input  [3:0] p1,
  input  [3:0] p2,
  input  [3:0] p3,
  input  [1:0] Select,
  output [3:0] Y
);

  wire [3:0] and_1_out, and_2_out, and_3_out, and_4_out, not_1_out, not_2_out, not_3_out, not_4_out;

  assign not_1_out = ~{4{Select[0]}};  // NOT_Gate not_1, 4 bits wide
  assign not_2_out = ~{4{Select[1]}};  // NOT_Gate not_2, 4 bits wide
  assign not_3_out = ~{4{Select[0]}};  // NOT_Gate not_3, 4 bits wide
  assign not_4_out = ~{4{Select[1]}};  // NOT_Gate not_4, 4 bits wide
  assign and_1_out = p0 & not_1_out & not_2_out;  // AND_Gate and_1, 4 bits wide
  assign and_2_out = p2 & not_3_out & {4{Select[1]}};  // AND_Gate and_2, 4 bits wide
  assign and_3_out = p1 & {4{Select[0]}} & not_4_out;  // AND_Gate and_3, 4 bits wide
  assign and_4_out = p3 & {4{Select[0]}} & {4{Select[1]}};  // AND_Gate and_4, 4 bits wide
  assign Y = and_1_out | and_2_out | and_3_out | and_4_out;  // OR_Gate or_1, 4 bits wide
endmodule

module Mux_2 (
  input  [1:0] p0,
  input  [1:0] p1,
  input  [1:0] p2,
  input  [1:0] p3,
  input  [1:0] Select,
  output [1:0] Y
);

  wire [1:0] and_1_out, and_2_out, and_3_out, and_4_out, not_1_out, not_2_out, not_3_out, not_4_out;

  assign not_1_out = ~{2{Select[0]}};  // NOT_Gate not_1, 2 bits wide
  assign not_2_out = ~{2{Select[1]}};  // NOT_Gate not_2, 2 bits wide
  assign not_3_out = ~{2{Select[0]}};  // NOT_Gate not_3, 2 bits wide
  assign not_4_out = ~{2{Select[1]}};  // NOT_Gate not_4, 2 bits wide
  assign and_1_out = p0 & not_1_out & not_2_out;  // AND_Gate and_1, 2 bits wide
  assign and_2_out = p2 & not_3_out & {2{Select[1]}};  // AND_Gate and_2, 2 bits wide
  assign and_3_out = p1 & {2{Select[0]}} & not_4_out;  // AND_Gate and_3, 2 bits wide
  assign and_4_out = p3 & {2{Select[0]}} & {2{Select[1]}};  // AND_Gate and_4, 2 bits wide
  assign Y = and_1_out | and_2_out | and_3_out | and_4_out;  // OR_Gate or_1, 2 bits wide
endmodule

module Mux_1 (
  input  p0,
  input  p1,
  input  p2,
  input  p3,
  input  [1:0] Select,
  output Y
);

  wire and_1_out, and_2_out, and_3_out, and_4_out, not_1_out, not_2_out, not_3_out, not_4_out;

  not not_1 (not_1_out, Select[0]);
  not not_2 (not_2_out, Select[1]);
  not not_3 (not_3_out, Select[0]);
  not not_4 (not_4_out, Select[1]);
  and and_1 (and_1_out, p0, not_1_out, not_2_out);
  and and_2 (and_2_out, p2, not_3_out, Select[1]);
  and and_3 (and_3_out, p1, Select[0], not_4_out);
  and and_4 (and_4_out, p3, Select[0], Select[1]);
  or or_1 (Y, and_1_out, and_2_out, and_3_out, and_4_out);
endmodule
