// Logisim project 8-1 Mux.circ as structural Verilog: 5 circuits, main circuit Mux_16
module Mux_16 (
  input  [15:0] p0,
  input  [15:0] p1,
  input  [15:0] p2,
  input  [15:0] p3,
  input  [15:0] p4,
  input  [15:0] p5,
  input  [15:0] p6,
  input  [15:0] p7,
  input  [2:0] s,
  output [15:0] o
);

  wire [15:0] mux_16_1_y, mux_16_2_y;

  _4_1_Mux_Mux_16 mux_16_1 (.Select(s[1:0]), .p2(p2), .p3(p3), .p0(p0), .p1(p1), .Y(mux_16_1_y));
  _4_1_Mux_Mux_16 mux_16_2 (.Select(s[1:0]), .p2(p6), .p3(p7), .p0(p4), .p1(p5), .Y(mux_16_2_y));
  _2_1_Mux_Mux_16 mux_16_3 (.p0(mux_16_1_y), .p1(mux_16_2_y), .Select(s[2]), .Y(o));
endmodule

module Mux_8 (
  input  [7:0] p0,
  input  [7:0] p1,
  input  [7:0] p2,
  input  [7:0] p3,
  input  [7:0] p4,
  input  [7:0] p5,
  input  [7:0] p6,
  input  [7:0] p7,
  input  [2:0] in_9,
  output [7:0] out_10
);

  wire [7:0] mux_8_1_y, mux_8_2_y;

  _4_1_Mux_Mux_8 mux_8_1 (.Select(in_9[1:0]), .p2(p2), .p3(p3), .p0(p0), .p1(p1), .Y(mux_8_1_y));
  _4_1_Mux_Mux_8 mux_8_2 (.Select(in_9[1:0]), .p2(p6), .p3(p7), .p0(p4), .p1(p5), .Y(mux_8_2_y));
  _2_1_Mux_Mux_8 mux_8_3 (.p0(mux_8_1_y), .p1(mux_8_2_y), .Select(in_9[2]), .Y(out_10));
endmodule

module Mux_4 (
  input  [3:0] p0,
  input  [3:0] p1,
  input  [3:0] p2,
  input  [3:0] p3,
  input  [3:0] p4,
  input  [3:0] p5,
  input  [3:0] p6,
  input  [3:0] p7,
  input  [2:0] in_9,
  output [3:0] out_10
);

  wire [3:0] mux_4_1_y, mux_4_2_y;

  _4_1_Mux_Mux_4 mux_4_1 (.Select(in_9[1:0]), .p2(p2), .p3(p3), .p0(p0), .p1(p1), .Y(mux_4_1_y));
  _4_1_Mux_Mux_4 mux_4_2 (.Select(in_9[1:0]), .p2(p6), .p3(p7), .p0(p4), .p1(p5), .Y(mux_4_2_y));
  _2_1_Mux_Mux_4 mux_4_3 (.p0(mux_4_1_y), .p1(mux_4_2_y), .Select(in_9[2]), .Y(out_10));
endmodule

module Mux_2 (
  input  [1:0] p0,
  input  [1:0] p1,
  input  [1:0] p2,
  input  [1:0] p3,
  input  [1:0] p4,
  input  [1:0] p5,
  input  [1:0] p6,
  input  [1:0] p7,
  input  [2:0] in_9,
  output [1:0] out_10
);

  wire [1:0] mux_2_1_y, mux_2_2_y;

  _4_1_Mux_Mux_2 mux_2_1 (.p2(p2), .p3(p3), .Select(in_9[1:0]), .p0(p0), .p1(p1), .Y(mux_2_1_y));
  _4_1_Mux_Mux_2 mux_2_2 (.p2(p6), .p3(p7), .Select(in_9[1:0]), .p0(p4), .p1(p5), .Y(mux_2_2_y));
  _2_1_Mux_Mux_2 mux_2_3 (.p0(mux_2_1_y), .p1(mux_2_2_y), .Select(in_9[2]), .Y(out_10));
endmodule

module Mux_1 (
  input  p0,
  input  p1,
  input  p2,
  input  p3,
  input  p4,
  input  p5,
  input  p6,
  input  p7,
  input  [2:0] in_9,
  output out_10
);

  wire mux_1_1_y, mux_1_2_y;

  _4_1_Mux_Mux_1 mux_1_1 (.Select(in_9[1:0]), .p2(p2), .p3(p3), .p0(p0), .p1(p1), .Y(mux_1_1_y));
  _4_1_Mux_Mux_1 mux_1_2 (.Select(in_9[1:0]), .p2(p6), .p3(p7), .p0(p4), .p1(p5), .Y(mux_1_2_y));
  _2_1_Mux_Mux_1 mux_1_3 (.p0(mux_1_1_y), .p1(mux_1_2_y), .Select(in_9[2]), .Y(out_10));
endmodule
