// Logisim project D Flip Flop.circ as structural Verilog: 1 circuit, main circuit D Flip Flop
module D_Flip_Flop (
  input  Clr,
  input  Clock,
  input  En,
  input  Data,
  output Output
);

  wire and_1_out, and_2_out, and_3_out, error_detector_1_1_out, nor_2_out, not_1_out, or_1_out,
       pulse_detect_1_pulse;

  Pulse_Detect pulse_detect_1 (.Clock(Clock), .Pulse(pulse_detect_1_pulse));
  and and_1 (and_1_out, pulse_detect_1_pulse, En);
  not not_1 (not_1_out, Data);
  and and_2 (and_2_out, and_1_out, not_1_out);
  and and_3 (and_3_out, and_1_out, Data);
  nor nor_1 (Output, and_2_out, Clr, or_1_out);
  or or_1 (or_1_out, nor_2_out, error_detector_1_1_out);
  Error_Detector__1 error_detector_1_1 (.In(nor_2_out), .Out(error_detector_1_1_out));
  nor nor_2 (nor_2_out, Output, and_3_out);

  // Notes on the sheet:
  //   En: pull=up
  //   Data: pull=down
endmodule
