// Logisim project JK Flip Flop.circ as structural Verilog: 1 circuit, main circuit JK Flip Flop
module JK_Flip_Flop (
  input  Clock,
  input  K,
  input  En,
  input  J,
  input  Clear,
  output Output
);

  wire and_1_out, and_2_out, and_3_out, and_4_out, error_detector_1_1_out, error_to_high_1_1_out,
       error_to_high_1_2_out, nor_1_out, pulse_detect_1_pulse;

  Pulse_Detect pulse_detect_1 (.Clock(Clock), .Pulse(pulse_detect_1_pulse));
  Error_to_high__1 error_to_high_1_1 (.In(nor_1_out), .Out(error_to_high_1_1_out));
  and and_1 (and_1_out, pulse_detect_1_pulse, En);
  Error_to_high__1 error_to_high_1_2 (.In(Output), .Out(error_to_high_1_2_out));
  and and_2 (and_2_out, error_to_high_1_1_out, K, and_1_out);
  and and_3 (and_3_out, and_1_out, J, error_to_high_1_2_out);
  nor nor_1 (nor_1_out, and_2_out, and_4_out);
  and and_4 (and_4_out, Output, ~Clear, ~error_detector_1_1_out);  // AND_Gate
  Error_Detector__1 error_detector_1_1 (.In(Output), .Out(error_detector_1_1_out));
  nor nor_2 (Output, nor_1_out, and_3_out);

  // Notes on the sheet:
  //   En: pull=up
  //   J: pull=down
  //   K: pull=down
endmodule
