// Logisim project SR Latch.circ as structural Verilog: 1 circuit, main circuit SR Latch
module SR_Latch (
  input  Reset,
  input  Set,
  output Output
);

  wire error_to_low_1_1_out, nor_2_out;

  nor nor_1 (Output, Reset, nor_2_out);
  Error_to_low__1 error_to_low_1_1 (.In(Output), .Out(error_to_low_1_1_out));
  nor nor_2 (nor_2_out, error_to_low_1_1_out, Set);

  // Notes on the sheet:
  //   Reset: pull=down
  //   Set: pull=down
endmodule
