// Logisim project Latch Register.circ as structural Verilog: 5 circuits, main circuit Latch Register (4)
module Latch_Register__1 (
  input  Clear,
  input  In,
  input  W,
  output Out
);

  wire and_1_out, not_1_out, z_detector_1_1_out_2;

  D_Latch d_latch_1 (.Data(In), .En(and_1_out), .Output(Out), .Clear(Clear));
  and and_1 (and_1_out, not_1_out, W);
  Z_Detector__1 z_detector_1_1 (.out_2(z_detector_1_1_out_2), .in_1(In));
  not not_1 (not_1_out, z_detector_1_1_out_2);
endmodule

module Latch_Register__2 (
  input  [1:0] In,
  input  Clear,
  input  W,
  output [1:0] Out
);

  wire and_1_out, not_1_out, z_detector_1_1_out_2;

  D_Latch d_latch_1 (.Data(In[0]), .En(and_1_out), .Output(Out[0]), .Clear(Clear));
  D_Latch d_latch_2 (.Data(In[1]), .En(and_1_out), .Output(Out[1]), .Clear(Clear));
  Z_Detector__1 z_detector_1_1 (.out_2(z_detector_1_1_out_2), .in_1(In[1]));
  not not_1 (not_1_out, z_detector_1_1_out_2);
  and and_1 (and_1_out, not_1_out, W);
endmodule

module Latch_Register__4 (
  input  [3:0] In,
  input  Clear,
  input  W,
  output [3:0] Out
);

  wire and_1_out, not_1_out, z_detector_1_1_out_2;

  D_Latch d_latch_1 (.Data(In[0]), .En(and_1_out), .Output(Out[0]), .Clear(Clear));
  D_Latch d_latch_2 (.Data(In[1]), .En(and_1_out), .Output(Out[1]), .Clear(Clear));
  D_Latch d_latch_3 (.Data(In[2]), .En(and_1_out), .Output(Out[2]), .Clear(Clear));
  D_Latch d_latch_4 (.Data(In[3]), .En(and_1_out), .Output(Out[3]), .Clear(Clear));
  Z_Detector__1 z_detector_1_1 (.out_2(z_detector_1_1_out_2), .in_1(In[3]));
  not not_1 (not_1_out, z_detector_1_1_out_2);
  and and_1 (and_1_out, not_1_out, W);
endmodule

module Latch_Register__8 (
  input  [7:0] In,
  input  Clear,
  input  W,
  output [7:0] Out
);

  wire d_latch_7_p2, not_1_out, z_detector_1_1_out_2;

  Z_Detector__1 z_detector_1_1 (.out_2(z_detector_1_1_out_2), .in_1(In[7]));
  not not_1 (not_1_out, z_detector_1_1_out_2);
  D_Latch d_latch_1 (.Data(In[0]), .En(d_latch_7_p2), .Output(Out[0]), .Clear(Clear));
  D_Latch d_latch_2 (.Data(In[1]), .En(d_latch_7_p2), .Output(Out[1]), .Clear(Clear));
  D_Latch d_latch_3 (.Data(In[2]), .En(d_latch_7_p2), .Output(Out[2]), .Clear(Clear));
  D_Latch d_latch_4 (.Data(In[3]), .En(d_latch_7_p2), .Output(Out[3]), .Clear(Clear));
  D_Latch d_latch_5 (.Data(In[4]), .En(d_latch_7_p2), .Output(Out[4]), .Clear(Clear));
  D_Latch d_latch_6 (.Data(In[5]), .En(d_latch_7_p2), .Output(Out[5]), .Clear(Clear));
  // D_Latch d_latch_7: pin names not known; wires that end beside it: In[6], d_latch_7_p2, Clear, Out[6]
  D_Latch d_latch_8 (.Data(In[7]), .En(d_latch_7_p2), .Output(Out[7]), .Clear(Clear));
  and and_1 (d_latch_7_p2, not_1_out, W);

  // Notes on the sheet:
  //   If bit 7 has high impedance, then enable is explicitly disabled
endmodule

module Latch_Register__16 (
  input  Clear,
  input  [15:0] In,
  input  W,
  output [15:0] Out
);

  wire and_1_out, Write, Z_1, Z_2, z_detector_1_1_out_2, z_detector_1_2_out_2;

  Z_Detector__1 z_detector_1_1 (.out_2(z_detector_1_1_out_2), .in_1(In[15]));
  not not_1 (Z_2, z_detector_1_1_out_2);
  and and_1 (and_1_out, Z_1, Z_2);
  D_Latch d_latch_1 (.Data(In[8]), .En(Write), .Output(Out[8]), .Clear(Clear));
  D_Latch d_latch_2 (.Data(In[9]), .En(Write), .Output(Out[9]), .Clear(Clear));
  D_Latch d_latch_3 (.Data(In[10]), .En(Write), .Output(Out[10]), .Clear(Clear));
  D_Latch d_latch_4 (.Data(In[11]), .En(Write), .Output(Out[11]), .Clear(Clear));
  D_Latch d_latch_5 (.Data(In[12]), .En(Write), .Output(Out[12]), .Clear(Clear));
  D_Latch d_latch_6 (.Data(In[13]), .En(Write), .Output(Out[13]), .Clear(Clear));
  D_Latch d_latch_7 (.Data(In[14]), .En(Write), .Output(Out[14]), .Clear(Clear));
  D_Latch d_latch_8 (.Data(In[15]), .En(Write), .Output(Out[15]), .Clear(Clear));
  and and_2 (Write, and_1_out, W);
  Z_Detector__1 z_detector_1_2 (.out_2(z_detector_1_2_out_2), .in_1(In[7]));
  not not_2 (Z_1, z_detector_1_2_out_2);
  D_Latch d_latch_9 (.Data(In[0]), .En(Write), .Output(Out[0]), .Clear(Clear));
  D_Latch d_latch_10 (.Data(In[1]), .En(Write), .Output(Out[1]), .Clear(Clear));
  D_Latch d_latch_11 (.Data(In[2]), .En(Write), .Output(Out[2]), .Clear(Clear));
  D_Latch d_latch_12 (.Data(In[3]), .En(Write), .Output(Out[3]), .Clear(Clear));
  D_Latch d_latch_13 (.Data(In[4]), .En(Write), .Output(Out[4]), .Clear(Clear));
  D_Latch d_latch_14 (.Data(In[5]), .En(Write), .Output(Out[5]), .Clear(Clear));
  D_Latch d_latch_15 (.Data(In[6]), .En(Write), .Output(Out[6]), .Clear(Clear));
  D_Latch d_latch_16 (.Data(In[7]), .En(Write), .Output(Out[7]), .Clear(Clear));

  // Other names for the same wires on the sheet: Clr = Clear; In_1[7:0] = In[7:0]; In_2[7:0] = In[15:8];
  //   Out_1[7:0] = Out[7:0]; Out_2[7:0] = Out[15:8]

  // Notes on the sheet:
  //   If bit 7 or 15 have high impedance, then enable is explicitly disabled
endmodule
