// Logisim project Priority Encoder.circ as structural Verilog: 5 circuits, main circuit 2-1 Priority Encoder
module _2_1_Priority_Encoder (
  input  [1:0] In,
  output V,
  output Out
);

  or or_1 (V, In[0], In[1]);

  assign Out = In[1];
endmodule

module _4_2_Priority_Encoder (
  input  [3:0] In,
  output V,
  output [1:0] Out
);

  wire and_1_out;

  or or_1 (V, In[0], In[2], In[3], In[1]);
  or or_2 (Out[1], In[2], In[3]);
  and and_1 (and_1_out, In[1], ~In[2]);  // AND_Gate
  or or_3 (Out[0], and_1_out, In[3]);
endmodule

module _8_3_Priority_Encoder (
  input  [7:0] In,
  output V,
  output [2:0] Out
);

  wire and_1_out, and_2_out, and_3_out, and_4_out, and_5_out;

  or or_1 (V, In[6], In[1], In[4], In[5], In[7], In[2], In[3], In[0]);
  and and_1 (and_1_out, ~In[6], ~In[4], ~In[2], In[1]);  // AND_Gate
  and and_2 (and_2_out, ~In[4], ~In[6], In[3]);  // AND_Gate
  and and_3 (and_3_out, ~In[6], In[5]);  // AND_Gate
  and and_4 (and_4_out, ~In[4], ~In[5], In[3]);  // AND_Gate
  and and_5 (and_5_out, ~In[5], ~In[4], In[2]);  // AND_Gate
  or or_2 (Out[0], In[7], and_1_out, and_2_out, and_3_out);
  or or_3 (Out[1], and_4_out, and_5_out, In[6], In[7]);
  or or_4 (Out[2], In[4], In[5], In[6], In[7]);
endmodule

module _16_4_Priority_Encoder (
  input  [15:0] in_1,
  output [3:0] Out,
  output V
);

  wire [1:0] n4_2_priority_encoder_1_out, n4_2_priority_encoder_2_out, n4_2_priority_encoder_3_out,
       n4_2_priority_encoder_4_out;
  wire [3:0] n4_2_priority_encoder_1_v;

  _4_2_Priority_Encoder u_4_2_priority_encoder_1 (
    .In(in_1[3:0]), .Out(n4_2_priority_encoder_1_out), .V(n4_2_priority_encoder_1_v[0]));
  _4_2_Priority_Encoder u_4_2_priority_encoder_2 (
    .In(in_1[7:4]), .Out(n4_2_priority_encoder_2_out), .V(n4_2_priority_encoder_1_v[1]));
  _4_2_Priority_Encoder u_4_2_priority_encoder_3 (
    .In(in_1[11:8]), .Out(n4_2_priority_encoder_3_out), .V(n4_2_priority_encoder_1_v[2]));
  _4_2_Priority_Encoder u_4_2_priority_encoder_4 (
    .In(in_1[15:12]), .Out(n4_2_priority_encoder_4_out), .V(n4_2_priority_encoder_1_v[3]));
  _4_1_Mux__2 u_4_1_mux_2_1 (
    ._0(n4_2_priority_encoder_1_out), ._1(n4_2_priority_encoder_2_out), ._2(n4_2_priority_encoder_3_out),
    ._3(n4_2_priority_encoder_4_out), .Select(Out[3:2]), .Y(Out[1:0]));
  _4_2_Priority_Encoder u_4_2_priority_encoder_5 (.In(n4_2_priority_encoder_1_v), .Out(Out[3:2]), .V(V));
endmodule

module _32_5_Priority_Encoder (
  input  [31:0] in_1,
  output [4:0] Out,
  output V
);

  wire [1:0] n16_4_priority_encoder_1_v;
  wire [3:0] n16_4_priority_encoder_1_out, n16_4_priority_encoder_2_out;

  _16_4_Priority_Encoder u_16_4_priority_encoder_1 (
    .in_1(in_1[15:0]), .Out(n16_4_priority_encoder_1_out), .V(n16_4_priority_encoder_1_v[0]));
  _16_4_Priority_Encoder u_16_4_priority_encoder_2 (
    .in_1(in_1[31:16]), .Out(n16_4_priority_encoder_2_out), .V(n16_4_priority_encoder_1_v[1]));
  _2_1_Mux__4 u_2_1_mux_4_1 (
    ._0(n16_4_priority_encoder_1_out), ._1(n16_4_priority_encoder_2_out), .Select(Out[4]), .Y(Out[3:0]));
  _2_1_Priority_Encoder u_2_1_priority_encoder_1 (.In(n16_4_priority_encoder_1_v), .Out(Out[4]), .V(V));
endmodule
