// Logisim project Left.circ as structural Verilog: 1 circuit, main circuit Left Shifter
module Left_Shifter (
  input  [7:0] in_1,
  output [7:0] out_2
);


  assign out_2 = {in_1[6:0], in_1[7]};
endmodule
