// Logisim project Right.circ as structural Verilog: 1 circuit, main circuit Right Shifter
module Right_Shifter (
  input  [7:0] in_1,
  output [7:0] out_2
);


  assign out_2 = {in_1[0], in_1[7:1]};
endmodule
